// Logisim project 实验1.circ as structural Verilog: 5 circuits, main circuit 一位二进制半加器
module \一位二进制半加器  (
  input  A,
  input  B,
  output S,
  output C
);

  xor xor_1 (S, A, B);
  and and_1 (C, A, B);
endmodule

module \一位二进制全加器  (
  input  A,
  input  B,
  input  C,
  output S,
  output C0
);

  wire nand_1_out, nand_2_out, nand_3_out;

  nand nand_1 (nand_1_out, A, B);
  nand nand_2 (nand_2_out, A, C);
  nand nand_3 (nand_3_out, B, C);
  xor xor_1 (S, A, B, C);
  nand nand_4 (C0, nand_1_out, nand_2_out, nand_3_out);
endmodule

module \串行进位并行加法器  (
  input  A0,
  input  B0,
  input  C0,
  input  A1,
  input  B1,
  input  A2,
  input  B2,
  input  A3,
  input  B3,
  output S0,
  output S1,
  output S2,
  output S3,
  output C4
);

  wire \一位二进制全加器_1_c0 , \一位二进制全加器_2_c0 , \一位二进制全加器_3_c0 ;

  \一位二进制全加器  \u_一位二进制全加器_1  (.S(S0), .C0(\一位二进制全加器_1_c0 ), .A(A0), .B(B0), .C(C0));
  \一位二进制全加器  \u_一位二进制全加器_2  (.S(S1), .C0(\一位二进制全加器_2_c0 ), .A(A1), .B(B1), .C(\一位二进制全加器_1_c0 ));
  \一位二进制全加器  \u_一位二进制全加器_3  (.S(S2), .C0(\一位二进制全加器_3_c0 ), .A(A2), .B(B2), .C(\一位二进制全加器_2_c0 ));
  \一位二进制全加器  \u_一位二进制全加器_4  (.S(S3), .C0(C4), .A(A3), .B(B3), .C(\一位二进制全加器_3_c0 ));
endmodule

module \先行进位并行加法器  (
  input  C0,
  input  A0,
  input  B0,
  input  A1,
  input  B1,
  input  A2,
  input  B2,
  input  A3,
  input  B3,
  output C4,
  output F3,
  output F2,
  output F1,
  output F0
);

  wire and_1_out, and_2_out, and_3_out, and_4_out, and_5_out, and_6_out, and_7_out, and_8_out, or_1_out,
       or_2_out, or_3_out, xor_1_out, xor_2_out, xor_3_out, xor_4_out;

  xor xor_1 (xor_1_out, A0, B0);
  and and_1 (and_1_out, A0, B0);
  xor xor_2 (xor_2_out, A1, B1);
  and and_2 (and_2_out, A1, B1);
  xor xor_3 (xor_3_out, A2, B2);
  and and_3 (and_3_out, A2, B2);
  xor xor_4 (xor_4_out, A3, B3);
  and and_4 (and_4_out, A3, B3);
  and and_5 (and_5_out, C0, xor_1_out);
  or or_1 (or_1_out, and_5_out, and_1_out);
  and and_6 (and_6_out, or_1_out, xor_2_out);
  or or_2 (or_2_out, and_6_out, and_2_out);
  and and_7 (and_7_out, or_2_out, xor_3_out);
  or or_3 (or_3_out, and_7_out, and_3_out);
  and and_8 (and_8_out, or_3_out, xor_4_out);
  or or_4 (C4, and_8_out, and_4_out);
  xor xor_5 (F3, or_3_out, xor_4_out);
  xor xor_6 (F2, or_2_out, xor_3_out);
  xor xor_7 (F1, or_1_out, xor_2_out);
  xor xor_8 (F0, C0, xor_1_out);
endmodule

module \线性进位并行加法器测试电路  (
  input  in_1,
  input  in_2,
  input  in_3,
  input  in_4,
  input  in_5,
  input  in_6,
  input  in_7,
  input  in_8,
  input  in_9,
  output out_10,
  output out_11,
  output out_12,
  output out_13,
  output out_14
);

  \先行进位并行加法器  \u_先行进位并行加法器_1  (
    .C0(in_1), .A0(in_5), .B0(in_9), .A1(in_4), .B1(in_8), .A2(in_3), .B2(in_7), .A3(in_2), .B3(in_6),
    .C4(out_14), .F1(out_12), .F0(out_13), .F2(out_11), .F3(out_10));
endmodule
