// Logisim project 实验2.circ as structural Verilog: 10 circuits, main circuit 四位二进制可逆计数器
module \先行进位并行加法器  (
  input  C0,
  input  A0,
  input  B0,
  input  A1,
  input  B1,
  input  A2,
  input  B2,
  input  A3,
  input  B3,
  output C4,
  output F3,
  output F2,
  output F1,
  output F0
);

  wire and_1_out, and_2_out, and_3_out, and_4_out, and_5_out, and_6_out, and_7_out, and_8_out, or_1_out,
       or_2_out, or_3_out, xor_1_out, xor_2_out, xor_3_out, xor_4_out;

  xor xor_1 (xor_1_out, A0, B0);
  and and_1 (and_1_out, A0, B0);
  xor xor_2 (xor_2_out, A1, B1);
  and and_2 (and_2_out, A1, B1);
  xor xor_3 (xor_3_out, A2, B2);
  and and_3 (and_3_out, A2, B2);
  xor xor_4 (xor_4_out, A3, B3);
  and and_4 (and_4_out, A3, B3);
  and and_5 (and_5_out, C0, xor_1_out);
  or or_1 (or_1_out, and_5_out, and_1_out);
  and and_6 (and_6_out, or_1_out, xor_2_out);
  or or_2 (or_2_out, and_6_out, and_2_out);
  and and_7 (and_7_out, or_2_out, xor_3_out);
  or or_3 (or_3_out, and_7_out, and_3_out);
  and and_8 (and_8_out, or_3_out, xor_4_out);
  or or_4 (C4, and_8_out, and_4_out);
  xor xor_5 (F3, or_3_out, xor_4_out);
  xor xor_6 (F2, or_2_out, xor_3_out);
  xor xor_7 (F1, or_1_out, xor_2_out);
  xor xor_8 (F0, C0, xor_1_out);
endmodule

module \四位二进制可逆计数器  (
  input  CPD,
  input  CPU,
  input  CLR,
  input  nLD,
  input  A,
  input  B,
  input  C,
  input  D,
  output QA,
  output QB,
  output QC,
  output QD
);

  wire and_1_out, and_2_out, and_3_out, and_4_out, and_5_out, and_6_out, and_7_out, and_8_out, and_9_out,
       and_10_out, and_11_out, and_12_out, and_13_out, and_14_out, d_ff_1_qn, d_ff_2_qn, d_ff_3_qn,
       d_ff_4_qn, not_1_out, not_2_out, not_3_out, not_4_out, not_5_out, or_1_out, or_2_out, or_3_out,
       or_4_out, or_5_out, or_6_out, or_7_out, or_8_out;

  or or_1 (or_1_out, CPD, CPU);
  not not_1 (not_1_out, nLD);
  not not_2 (not_2_out, A);
  not not_3 (not_3_out, B);
  not not_4 (not_4_out, C);
  not not_5 (not_5_out, D);
  and and_1 (and_1_out, d_ff_1_qn, CPD);
  and and_2 (and_2_out, QA, CPU);
  and and_3 (and_3_out, d_ff_1_qn, d_ff_2_qn, CPD);
  and and_4 (and_4_out, QA, QB, CPU);
  and and_5 (and_5_out, d_ff_1_qn, d_ff_2_qn, d_ff_3_qn, CPD);
  and and_6 (and_6_out, QA, QB, QC, CPU);
  or or_2 (or_2_out, and_1_out, and_2_out);
  or or_3 (or_3_out, and_3_out, and_4_out);
  or or_4 (or_4_out, and_5_out, and_6_out);
  and and_7 (and_7_out, not_1_out, A);
  and and_8 (and_8_out, not_1_out, not_2_out);
  or or_5 (or_5_out, and_8_out, CLR);
  and and_9 (and_9_out, not_1_out, B);
  and and_10 (and_10_out, not_1_out, not_3_out);
  or or_6 (or_6_out, and_10_out, CLR);
  and and_11 (and_11_out, not_1_out, C);
  and and_12 (and_12_out, not_1_out, not_4_out);
  or or_7 (or_7_out, and_12_out, CLR);
  and and_13 (and_13_out, not_1_out, D);
  and and_14 (and_14_out, not_1_out, not_5_out);
  or or_8 (or_8_out, and_14_out, CLR);
  D_Flip_Flop #(.trigger("falling"), .Pre_Clr_Positions("LEGACY"), .NegatePresetClear("false"), .enable("true"), .NewFFLayout("true")) d_ff_1 (
    .clk(or_1_out), .D(d_ff_1_qn), .Q(QA), .Qn(d_ff_1_qn), .preset(and_7_out), .en(nLD), .reset(or_5_out));
  D_Flip_Flop #(.trigger("falling"), .Pre_Clr_Positions("LEGACY"), .NegatePresetClear("false"), .enable("true"), .NewFFLayout("true")) d_ff_2 (
    .clk(or_2_out), .D(d_ff_2_qn), .Q(QB), .Qn(d_ff_2_qn), .preset(and_9_out), .en(nLD), .reset(or_6_out));
  D_Flip_Flop #(.trigger("falling"), .Pre_Clr_Positions("LEGACY"), .NegatePresetClear("false"), .enable("true"), .NewFFLayout("true")) d_ff_3 (
    .clk(or_3_out), .D(d_ff_3_qn), .Q(QC), .Qn(d_ff_3_qn), .preset(and_11_out), .en(nLD), .reset(or_7_out));
  D_Flip_Flop #(.trigger("falling"), .Pre_Clr_Positions("LEGACY"), .NegatePresetClear("false"), .enable("true"), .NewFFLayout("true")) d_ff_4 (
    .clk(or_4_out), .D(d_ff_4_qn), .Q(QD), .Qn(d_ff_4_qn), .preset(and_13_out), .en(nLD), .reset(or_8_out));
endmodule

module \四位二进制可逆计数器测试电路  (
  input  in_1,
  input  in_2,
  input  in_3,
  input  in_4,
  input  in_5,
  input  in_6,
  input  in_7,
  input  in_8,
  output out_9,
  output out_10,
  output out_11,
  output out_12
);

  \四位二进制可逆计数器  \u_四位二进制可逆计数器_1  (
    .CPD(in_3), .CPU(in_1), .CLR(in_2), .nLD(in_8), .A(in_7), .B(in_6), .C(in_5), .D(in_4), .QA(out_12),
    .QB(out_11), .QC(out_10), .QD(out_9));
endmodule

module \二进制转8421码电路  (
  input  I1,
  input  I2,
  input  I3,
  input  I4,
  output O5,
  output O6,
  output O7,
  output O8,
  output O1,
  output O2,
  output O3,
  output O4
);

  wire and_1_out, or_1_out;

  or or_1 (or_1_out, I2, I3);
  and and_1 (and_1_out, I1, or_1_out);
  \先行进位并行加法器  \u_先行进位并行加法器_1  (
    .C0(1'b0), .A0(I4), .B0(1'b0), .A1(I3), .B1(and_1_out), .A2(I2), .B2(and_1_out), .A3(I1), .B3(1'b0),
    .C4(O4), .F1(O7), .F0(O8), .F2(O6), .F3(O5));

  assign O1 = 1'b0;
  assign O2 = 1'b0;
  assign O3 = 1'b0;
endmodule

module \二进制转8421码电路测试电路  (
  input  in_1,
  input  in_2,
  input  in_3,
  input  in_4,
  output out_5,
  output out_6,
  output out_7,
  output out_8,
  output out_9,
  output out_10,
  output out_11,
  output out_12
);

  \二进制转8421码电路  \u_二进制转8421码电路_1  (
    .I1(in_1), .I2(in_2), .I3(in_3), .I4(in_4), .O5(out_9), .O6(out_10), .O7(out_11), .O8(out_12),
    .O1(out_5), .O2(out_6), .O3(out_7), .O4(out_8));
endmodule

module \显示电路  (
  input  A3,
  input  A2,
  input  A1,
  input  A0,
  output a,
  output b,
  output c,
  output d,
  output e,
  output f,
  output g
);

  wire and_1_out, and_2_out, and_3_out, and_4_out, and_5_out, and_6_out, and_7_out, and_8_out, and_9_out,
       and_10_out, and_11_out, and_12_out, and_13_out, and_14_out, and_15_out, and_16_out, and_17_out,
       and_18_out, and_19_out, and_20_out, and_21_out, and_22_out, and_23_out, and_24_out, and_25_out,
       not_1_out, not_2_out, not_3_out, not_4_out;

  not not_1 (not_1_out, A3);
  not not_2 (not_2_out, A2);
  not not_3 (not_3_out, A1);
  not not_4 (not_4_out, A0);
  and and_1 (and_1_out, not_1_out, not_2_out, not_4_out);
  and and_2 (and_2_out, not_1_out, A1);
  and and_3 (and_3_out, not_1_out, A2, A0);
  and and_4 (and_4_out, A3, not_3_out);
  and and_5 (and_5_out, not_1_out, not_2_out);
  and and_6 (and_6_out, not_1_out, not_3_out, not_4_out);
  and and_7 (and_7_out, not_2_out, not_3_out);
  and and_8 (and_8_out, not_1_out, A1, A0);
  and and_9 (and_9_out, not_2_out, not_3_out);
  and and_10 (and_10_out, not_1_out, A0);
  and and_11 (and_11_out, not_1_out, A2);
  and and_12 (and_12_out, not_2_out, not_3_out, not_4_out);
  and and_13 (and_13_out, not_1_out, not_2_out, A1);
  and and_14 (and_14_out, not_1_out, A1, not_4_out);
  and and_15 (and_15_out, not_1_out, A2, not_3_out, A0);
  and and_16 (and_16_out, not_2_out, not_3_out, not_4_out);
  and and_17 (and_17_out, not_1_out, A1, not_4_out);
  and and_18 (and_18_out, not_1_out, not_3_out, not_4_out);
  and and_19 (and_19_out, not_1_out, A2, not_3_out);
  and and_20 (and_20_out, not_1_out, A2, not_4_out);
  and and_21 (and_21_out, A3, not_2_out, not_3_out);
  and and_22 (and_22_out, not_1_out, not_2_out, A1);
  and and_23 (and_23_out, not_1_out, A2, not_3_out);
  and and_24 (and_24_out, not_1_out, A2, not_4_out);
  and and_25 (and_25_out, A3, not_2_out, not_3_out);
  or or_1 (a, and_1_out, and_2_out, and_3_out, and_4_out);
  or or_2 (b, and_5_out, and_6_out, and_7_out, and_8_out);
  or or_3 (c, and_9_out, and_10_out, and_11_out);
  or or_4 (d, and_12_out, and_13_out, and_14_out, and_15_out);
  or or_5 (e, and_16_out, and_17_out);
  or or_6 (f, and_18_out, and_19_out, and_20_out, and_21_out);
  or or_7 (g, and_22_out, and_23_out, and_24_out, and_25_out);
endmodule

module \显示电路测试电路  (
  input  A3,
  input  A2,
  input  A1,
  input  A0
);

  wire \二进制转8421码电路_1_o1 , \二进制转8421码电路_1_o2 , \二进制转8421码电路_1_o3 , \二进制转8421码电路_1_o4 , \二进制转8421码电路_1_o5 ,
       \二进制转8421码电路_1_o6 , \二进制转8421码电路_1_o7 , \二进制转8421码电路_1_o8 , \显示电路_1_a , \显示电路_1_b , \显示电路_1_c ,
       \显示电路_1_d , \显示电路_1_e , \显示电路_1_f , \显示电路_1_g , \显示电路_2_a , \显示电路_2_b , \显示电路_2_c , \显示电路_2_d ,
       \显示电路_2_e , \显示电路_2_f , \显示电路_2_g ;

  \二进制转8421码电路  \u_二进制转8421码电路_1  (
    .I1(A3), .I2(A2), .I3(A1), .I4(A0), .O5(\二进制转8421码电路_1_o5 ), .O6(\二进制转8421码电路_1_o6 ),
    .O7(\二进制转8421码电路_1_o7 ), .O8(\二进制转8421码电路_1_o8 ), .O1(\二进制转8421码电路_1_o1 ), .O2(\二进制转8421码电路_1_o2 ),
    .O3(\二进制转8421码电路_1_o3 ), .O4(\二进制转8421码电路_1_o4 ));
  \显示电路  \u_显示电路_1  (
    .A3(\二进制转8421码电路_1_o1 ), .A2(\二进制转8421码电路_1_o2 ), .A1(\二进制转8421码电路_1_o3 ), .A0(\二进制转8421码电路_1_o4 ),
    .a(\显示电路_1_a ), .b(\显示电路_1_b ), .c(\显示电路_1_c ), .d(\显示电路_1_d ), .e(\显示电路_1_e ), .f(\显示电路_1_f ),
    .g(\显示电路_1_g ));
  \显示电路  \u_显示电路_2  (
    .A3(\二进制转8421码电路_1_o5 ), .A2(\二进制转8421码电路_1_o6 ), .A1(\二进制转8421码电路_1_o7 ), .A0(\二进制转8421码电路_1_o8 ),
    .a(\显示电路_2_a ), .b(\显示电路_2_b ), .c(\显示电路_2_c ), .d(\显示电路_2_d ), .e(\显示电路_2_e ), .f(\显示电路_2_f ),
    .g(\显示电路_2_g ));
  _7_Segment_Display #(.active("true")) u_7_segment_display_1 (
    .g(\显示电路_1_g ), .f(\显示电路_1_f ), .a(\显示电路_1_a ), .b(\显示电路_1_b ), .e(\显示电路_1_e ), .d(\显示电路_1_d ),
    .c(\显示电路_1_c ));  // open: dp
  _7_Segment_Display #(.active("true")) u_7_segment_display_2 (
    .g(\显示电路_2_g ), .f(\显示电路_2_f ), .a(\显示电路_2_a ), .b(\显示电路_2_b ), .e(\显示电路_2_e ), .d(\显示电路_2_d ),
    .c(\显示电路_2_c ));  // open: dp
endmodule

module \报警电路  (
  input  CPU,
  input  CLR,
  input  CPD,
  input  D,
  input  C,
  input  B,
  input  A,
  input  nLD
);

  wire and_1_out, and_2_out, and_3_out, and_4_out, not_1_out, or_1_out, \四位二进制可逆计数器_1_qa , \四位二进制可逆计数器_1_qb ,
       \四位二进制可逆计数器_1_qc , \四位二进制可逆计数器_1_qd ;

  and and_1 (and_1_out, not_1_out, CPU);
  and and_2 (and_2_out, CPD, or_1_out);
  not not_1 (not_1_out, and_3_out);
  \四位二进制可逆计数器  \u_四位二进制可逆计数器_1  (
    .CPD(and_2_out), .CPU(and_1_out), .CLR(CLR), .nLD(nLD), .A(A), .B(B), .C(C), .D(D),
    .QA(\四位二进制可逆计数器_1_qa ), .QB(\四位二进制可逆计数器_1_qb ), .QC(\四位二进制可逆计数器_1_qc ), .QD(\四位二进制可逆计数器_1_qd ));
  and and_3 (and_3_out, \四位二进制可逆计数器_1_qd , \四位二进制可逆计数器_1_qc , \四位二进制可逆计数器_1_qb , \四位二进制可逆计数器_1_qa );
  or or_1 (or_1_out, \四位二进制可逆计数器_1_qd , \四位二进制可逆计数器_1_qc , \四位二进制可逆计数器_1_qb , \四位二进制可逆计数器_1_qa );
  LED #(.active("true")) led_1 (.in(and_4_out));
  and and_4 (and_4_out, CPU, and_3_out);
  // Buzzer #(.freq_measure("Hz"), .vol_width(7)) buzzer_1: pin names not known; wires that end beside it: and_4_out
endmodule

module \小型实验室门禁系统  (
  input  in_1,
  input  in_2,
  input  in_3,
  output out_4,
  output out_5,
  output out_6,
  output out_7,
  output out_8,
  output out_9,
  output out_10,
  output out_11,
  output out_12,
  output out_13,
  output out_14,
  output out_15,
  output out_16,
  output out_17,
  output out_18
);

  wire and_1_out, and_2_out, and_3_out, not_1_out, or_1_out, \二进制转8421码电路_1_o1 , \二进制转8421码电路_1_o2 ,
       \二进制转8421码电路_1_o3 , \二进制转8421码电路_1_o4 , \二进制转8421码电路_1_o5 , \二进制转8421码电路_1_o6 , \二进制转8421码电路_1_o7 ,
       \二进制转8421码电路_1_o8 , \四位二进制可逆计数器_1_qa , \四位二进制可逆计数器_1_qb , \四位二进制可逆计数器_1_qc , \四位二进制可逆计数器_1_qd ;

  \显示电路  \u_显示电路_1  (
    .A3(\二进制转8421码电路_1_o1 ), .A2(\二进制转8421码电路_1_o2 ), .A1(\二进制转8421码电路_1_o3 ), .A0(\二进制转8421码电路_1_o4 ),
    .a(out_4), .b(out_5), .c(out_6), .d(out_7), .e(out_8), .f(out_9), .g(out_10));
  \二进制转8421码电路  \u_二进制转8421码电路_1  (
    .I1(\四位二进制可逆计数器_1_qd ), .I2(\四位二进制可逆计数器_1_qc ), .I3(\四位二进制可逆计数器_1_qb ), .I4(\四位二进制可逆计数器_1_qa ),
    .O5(\二进制转8421码电路_1_o5 ), .O6(\二进制转8421码电路_1_o6 ), .O7(\二进制转8421码电路_1_o7 ), .O8(\二进制转8421码电路_1_o8 ),
    .O1(\二进制转8421码电路_1_o1 ), .O2(\二进制转8421码电路_1_o2 ), .O3(\二进制转8421码电路_1_o3 ), .O4(\二进制转8421码电路_1_o4 ));
  \显示电路  \u_显示电路_2  (
    .A3(\二进制转8421码电路_1_o5 ), .A2(\二进制转8421码电路_1_o6 ), .A1(\二进制转8421码电路_1_o7 ), .A0(\二进制转8421码电路_1_o8 ),
    .a(out_11), .b(out_12), .c(out_13), .d(out_14), .e(out_15), .f(out_16), .g(out_17));
  and and_1 (and_1_out, not_1_out, in_1);
  and and_2 (and_2_out, in_3, or_1_out);
  not not_1 (not_1_out, and_3_out);
  \四位二进制可逆计数器  \u_四位二进制可逆计数器_1  (
    .CPD(and_2_out), .CPU(and_1_out), .CLR(in_2), .nLD(1'b1), .A(1'b0), .B(1'b0), .C(1'b0), .D(1'b0),
    .QA(\四位二进制可逆计数器_1_qa ), .QB(\四位二进制可逆计数器_1_qb ), .QC(\四位二进制可逆计数器_1_qc ), .QD(\四位二进制可逆计数器_1_qd ));
  and and_3 (and_3_out, \四位二进制可逆计数器_1_qd , \四位二进制可逆计数器_1_qc , \四位二进制可逆计数器_1_qb , \四位二进制可逆计数器_1_qa );
  or or_1 (or_1_out, \四位二进制可逆计数器_1_qd , \四位二进制可逆计数器_1_qc , \四位二进制可逆计数器_1_qb , \四位二进制可逆计数器_1_qa );
  and and_4 (out_18, in_1, and_3_out);
endmodule

module \小型实验室门禁系统测试电路  (
  input  CPU,
  input  CLR,
  input  CPD
);

  wire \小型实验室门禁系统_1_out_4 , \小型实验室门禁系统_1_out_5 , \小型实验室门禁系统_1_out_6 , \小型实验室门禁系统_1_out_7 ,
       \小型实验室门禁系统_1_out_8 , \小型实验室门禁系统_1_out_9 , \小型实验室门禁系统_1_out_10 , \小型实验室门禁系统_1_out_11 ,
       \小型实验室门禁系统_1_out_12 , \小型实验室门禁系统_1_out_13 , \小型实验室门禁系统_1_out_14 , \小型实验室门禁系统_1_out_15 ,
       \小型实验室门禁系统_1_out_16 , \小型实验室门禁系统_1_out_17 , \小型实验室门禁系统_1_out_18 ;

  _7_Segment_Display #(.active("true")) u_7_segment_display_1 (
    .g(\小型实验室门禁系统_1_out_10 ), .f(\小型实验室门禁系统_1_out_9 ), .a(\小型实验室门禁系统_1_out_4 ), .b(\小型实验室门禁系统_1_out_5 ),
    .e(\小型实验室门禁系统_1_out_8 ), .d(\小型实验室门禁系统_1_out_7 ), .c(\小型实验室门禁系统_1_out_6 ));  // open: dp
  \小型实验室门禁系统  \u_小型实验室门禁系统_1  (
    .in_1(CPU), .in_2(CLR), .in_3(CPD), .out_18(\小型实验室门禁系统_1_out_18 ), .out_4(\小型实验室门禁系统_1_out_4 ),
    .out_5(\小型实验室门禁系统_1_out_5 ), .out_6(\小型实验室门禁系统_1_out_6 ), .out_7(\小型实验室门禁系统_1_out_7 ),
    .out_8(\小型实验室门禁系统_1_out_8 ), .out_9(\小型实验室门禁系统_1_out_9 ), .out_10(\小型实验室门禁系统_1_out_10 ),
    .out_11(\小型实验室门禁系统_1_out_11 ), .out_12(\小型实验室门禁系统_1_out_12 ), .out_13(\小型实验室门禁系统_1_out_13 ),
    .out_14(\小型实验室门禁系统_1_out_14 ), .out_15(\小型实验室门禁系统_1_out_15 ), .out_16(\小型实验室门禁系统_1_out_16 ),
    .out_17(\小型实验室门禁系统_1_out_17 ));
  _7_Segment_Display #(.active("true")) u_7_segment_display_2 (
    .g(\小型实验室门禁系统_1_out_17 ), .f(\小型实验室门禁系统_1_out_16 ), .a(\小型实验室门禁系统_1_out_11 ), .b(\小型实验室门禁系统_1_out_12 ),
    .e(\小型实验室门禁系统_1_out_15 ), .d(\小型实验室门禁系统_1_out_14 ), .c(\小型实验室门禁系统_1_out_13 ));  // open: dp
  LED #(.active("true")) led_1 (.in(\小型实验室门禁系统_1_out_18 ));
  // Buzzer #(.freq_measure("Hz"), .vol_width(7)) buzzer_1: pin names not known; wires that end beside it: \小型实验室门禁系统_1_out_18 
endmodule
