// Logisim project 实验3.circ as structural Verilog: 6 circuits, main circuit 四位乘法器
module \四位乘法器  (
  input  [3:0] in_1,
  input  [3:0] in_2,
  output [7:0] out_3
);

  wire [7:0] adder_1_out, adder_2_out, adder_3_out, adder_4_out, bit_extender_1_out, multiplexer_1_out,
       multiplexer_2_out, multiplexer_3_out, shifter_1_out, shifter_2_out, shifter_3_out;

  assign bit_extender_1_out = {{4{1'b0}}, in_2};  // Bit_Extender bit_extender_1
  Adder #(.width(8)) adder_1 (.a({8{1'b0}}), .b(bit_extender_1_out), .out(adder_1_out));  // open: cin, cout
  Shifter #(.width(8), .shift("ll")) shifter_1 (.in(bit_extender_1_out), .\dist (3'b001), .out(shifter_1_out));
  Multiplexer #(.select(1), .width(8), .disabled("Z"), .enable("false")) multiplexer_1 (
    .in0({8{1'b0}}), .in1(adder_1_out), .out(multiplexer_1_out), .sel(in_1[0]));
  Adder #(.width(8)) adder_2 (.a(multiplexer_1_out), .b(shifter_1_out), .out(adder_2_out));  // open: cin, cout
  Shifter #(.width(8), .shift("ll")) shifter_2 (.in(shifter_1_out), .\dist (3'b001), .out(shifter_2_out));
  Multiplexer #(.select(1), .width(8), .disabled("Z"), .enable("false")) multiplexer_2 (
    .in0(multiplexer_1_out), .in1(adder_2_out), .out(multiplexer_2_out), .sel(in_1[1]));
  Adder #(.width(8)) adder_3 (.a(multiplexer_2_out), .b(shifter_2_out), .out(adder_3_out));  // open: cin, cout
  Shifter #(.width(8), .shift("ll")) shifter_3 (.in(shifter_2_out), .\dist (3'b001), .out(shifter_3_out));
  Multiplexer #(.select(1), .width(8), .disabled("Z"), .enable("false")) multiplexer_3 (
    .in0(multiplexer_2_out), .in1(adder_3_out), .out(multiplexer_3_out), .sel(in_1[2]));
  Adder #(.width(8)) adder_4 (.a(multiplexer_3_out), .b(shifter_3_out), .out(adder_4_out));  // open: cin, cout
  Shifter #(.width(8), .shift("ll")) shifter_4 (.in(shifter_3_out), .\dist (3'b001));  // open: out
  Multiplexer #(.select(1), .width(8), .disabled("Z"), .enable("false")) multiplexer_4 (
    .in0(multiplexer_3_out), .in1(adder_4_out), .out(out_3), .sel(in_1[3]));
endmodule

module \四位乘法器测试电路  (
  input  [3:0] a_3_0,
  input  [3:0] b_3_0,
  output [7:0] p_7_0
);

  \四位乘法器  \u_四位乘法器_1  (.in_2(b_3_0), .out_3(p_7_0), .in_1(a_3_0));
endmodule

module \_32X4乘法器  (
  input  [3:0] in_1,
  input  [31:0] in_2,
  output [31:0] out_3
);

  wire [31:0] adder_1_out, adder_2_out, adder_3_out, adder_4_out, multiplexer_1_out, multiplexer_2_out,
       multiplexer_3_out, shifter_1_out, shifter_2_out, shifter_3_out;

  Adder #(.width(32)) adder_1 (.a({32{1'b0}}), .b(in_2), .out(adder_1_out));  // open: cin, cout
  Shifter #(.width(32), .shift("ll")) shifter_1 (.in(in_2), .\dist (5'b00001), .out(shifter_1_out));
  Multiplexer #(.select(1), .width(32), .disabled("Z"), .enable("false")) multiplexer_1 (
    .in0({32{1'b0}}), .in1(adder_1_out), .out(multiplexer_1_out), .sel(in_1[0]));
  Adder #(.width(32)) adder_2 (.a(multiplexer_1_out), .b(shifter_1_out), .out(adder_2_out));  // open: cin, cout
  Shifter #(.width(32), .shift("ll")) shifter_2 (.in(shifter_1_out), .\dist (5'b00001), .out(shifter_2_out));
  Multiplexer #(.select(1), .width(32), .disabled("Z"), .enable("false")) multiplexer_2 (
    .in0(multiplexer_1_out), .in1(adder_2_out), .out(multiplexer_2_out), .sel(in_1[1]));
  Adder #(.width(32)) adder_3 (.a(multiplexer_2_out), .b(shifter_2_out), .out(adder_3_out));  // open: cin, cout
  Shifter #(.width(32), .shift("ll")) shifter_3 (.in(shifter_2_out), .\dist (5'b00001), .out(shifter_3_out));
  Multiplexer #(.select(1), .width(32), .disabled("Z"), .enable("false")) multiplexer_3 (
    .in0(multiplexer_2_out), .in1(adder_3_out), .out(multiplexer_3_out), .sel(in_1[2]));
  Adder #(.width(32)) adder_4 (.a(multiplexer_3_out), .b(shifter_3_out), .out(adder_4_out));  // open: cin, cout
  Shifter #(.width(32), .shift("ll")) shifter_4 (.in(shifter_3_out), .\dist (5'b00001));  // open: out
  Multiplexer #(.select(1), .width(32), .disabled("Z"), .enable("false")) multiplexer_4 (
    .in0(multiplexer_3_out), .in1(adder_4_out), .out(out_3), .sel(in_1[3]));
endmodule

module \_32X4乘法器测试电路  (
  input  [3:0] in_1,
  input  [31:0] in_2,
  output [31:0] out_3
);

  \_32X4乘法器  \u_32x4乘法器_1  (.in_2(in_2), .out_3(out_3), .in_1(in_1));
endmodule

module \_32X32位乘法器  (
  input  [31:0] in_1,
  input  [31:0] in_2,
  output [31:0] out_3
);

  wire [3:0] \n32x4乘法器_3_out_3 , \n32x4乘法器_3_out_3_3 , \n32x4乘法器_3_out_3_4 , \n32x4乘法器_3_out_3_5 ,
       \n32x4乘法器_3_out_3_6 , \n32x4乘法器_3_out_3_7 , \n32x4乘法器_3_out_3_8 , \n32x4乘法器_4_out_3 ,
       \n32x4乘法器_4_out_3_2 , \n32x4乘法器_4_out_3_3 , \n32x4乘法器_4_out_3_4 , \n32x4乘法器_4_out_3_5 ,
       \n32x4乘法器_4_out_3_7 , \n32x4乘法器_4_out_3_8 ;
  wire [31:0] adder_1_out, adder_2_out, adder_3_out, adder_4_out, adder_5_out, adder_6_out,
       \n32x4乘法器_1_out_3 , \n32x4乘法器_2_out_3 , \n32x4乘法器_5_out_3 , \n32x4乘法器_6_out_3 , \n32x4乘法器_7_out_3 ,
       \n32x4乘法器_8_out_3 ;
  wire [31:28] \n32x4乘法器_3_out_3_2 , \n32x4乘法器_4_out_3_6 ;

  \_32X4乘法器  \u_32x4乘法器_1  (.in_2(in_2), .out_3(\n32x4乘法器_1_out_3 ), .in_1(in_1[15:12]));
  \_32X4乘法器  \u_32x4乘法器_2  (.in_2(in_2), .out_3(\n32x4乘法器_2_out_3 ), .in_1(in_1[31:28]));
  \_32X4乘法器  \u_32x4乘法器_3  (
    .in_2(in_2),
    .out_3({\n32x4乘法器_3_out_3_2 , \n32x4乘法器_3_out_3 , \n32x4乘法器_3_out_3_8 , \n32x4乘法器_3_out_3_7 , \n32x4乘法器_3_out_3_6 , \n32x4乘法器_3_out_3_5 , \n32x4乘法器_3_out_3_4 , \n32x4乘法器_3_out_3_3 }),
    .in_1(in_1[11:8]));
  \_32X4乘法器  \u_32x4乘法器_4  (
    .in_2(in_2),
    .out_3({\n32x4乘法器_4_out_3_6 , \n32x4乘法器_4_out_3_5 , \n32x4乘法器_4_out_3_4 , \n32x4乘法器_4_out_3_3 , \n32x4乘法器_4_out_3_2 , \n32x4乘法器_4_out_3 , \n32x4乘法器_4_out_3_8 , \n32x4乘法器_4_out_3_7 }),
    .in_1(in_1[27:24]));
  \_32X4乘法器  \u_32x4乘法器_5  (.in_2(in_2), .out_3(\n32x4乘法器_5_out_3 ), .in_1(in_1[7:4]));
  \_32X4乘法器  \u_32x4乘法器_6  (.in_2(in_2), .out_3(\n32x4乘法器_6_out_3 ), .in_1(in_1[23:20]));
  \_32X4乘法器  \u_32x4乘法器_7  (.in_2(in_2), .out_3(\n32x4乘法器_7_out_3 ), .in_1(in_1[3:0]));
  \_32X4乘法器  \u_32x4乘法器_8  (.in_2(in_2), .out_3(\n32x4乘法器_8_out_3 ), .in_1(in_1[19:16]));
  Adder #(.width(32)) adder_1 (
    .a(\n32x4乘法器_7_out_3 ), .b({\n32x4乘法器_5_out_3 [27:0], 4'b0000}), .out(adder_1_out));  // open: cin, cout
  Adder #(.width(32)) adder_2 (
    .a({\n32x4乘法器_3_out_3_8 , \n32x4乘法器_3_out_3_7 , \n32x4乘法器_3_out_3_6 , \n32x4乘法器_3_out_3_5 , \n32x4乘法器_3_out_3_4 , \n32x4乘法器_3_out_3_3 , {8{1'b0}}}),
    .b({\n32x4乘法器_1_out_3 [19:0], {12{1'b0}}}), .out(adder_2_out));  // open: cin, cout
  Adder #(.width(32)) adder_3 (
    .a({\n32x4乘法器_8_out_3 [15:0], {16{1'b0}}}), .b({\n32x4乘法器_6_out_3 [11:0], {20{1'b0}}}), .out(adder_3_out));  // open: cin, cout
  Adder #(.width(32)) adder_4 (
    .a({\n32x4乘法器_4_out_3_8 , \n32x4乘法器_4_out_3_7 , {24{1'b0}}}), .b({\n32x4乘法器_2_out_3 [3:0], {28{1'b0}}}),
    .out(adder_4_out));  // open: cin, cout
  Adder #(.width(32)) adder_5 (.a(adder_1_out), .b(adder_2_out), .out(adder_5_out));  // open: cin, cout
  Adder #(.width(32)) adder_6 (.a(adder_3_out), .b(adder_4_out), .out(adder_6_out));  // open: cin, cout
  Adder #(.width(32)) adder_7 (.a(adder_5_out), .b(adder_6_out), .out(out_3));  // open: cin, cout
endmodule

module \_32X32位乘法器测试电路  (
  input  [31:0] in_1,
  input  [31:0] in_2,
  output [31:0] out_3
);

  \_32X32位乘法器  \u_32x32位乘法器_1  (.in_1(in_1), .in_2(in_2), .out_3(out_3));
endmodule
