// Logisim project 实验4.circ as structural Verilog: 4 circuits, main circuit 四位除法器
module \四位除法器  (
  input  [3:0] n2,
  input  [3:0] d,
  output [3:0] quot,
  output [3:0] rem
);

  wire comparator_1_eq, comparator_1_gt, comparator_2_eq, comparator_2_gt, comparator_3_eq, comparator_3_gt,
       comparator_4_eq, comparator_4_gt, or_1_out, or_2_out, or_3_out, or_4_out;
  wire [1:1] multiplexer_3_out;
  wire [3:0] multiplexer_1_out, multiplexer_2_out, multiplexer_3_out_2, multiplexer_5_out, multiplexer_6_out,
       subtractor_1_out, subtractor_2_out, subtractor_3_out, subtractor_4_out;
  wire [7:0] shifter_1_out, shifter_2_out_2, shifter_3_out, shifter_4_out;
  wire [7:4] shifter_2_out;

  Shifter #(.width(8), .shift("ll")) shifter_1 (.in({4'b0000, n2}), .\dist (3'b001), .out(shifter_1_out));
  Subtractor #(.width(4)) subtractor_1 (.a(shifter_1_out[7:4]), .b(d), .out(subtractor_1_out));  // open: bin, bout
  Comparator #(.width(4), .mode("unsigned")) comparator_1 (
    .a(shifter_1_out[7:4]), .b(d), .gt(comparator_1_gt), .eq(comparator_1_eq));  // open: lt
  Multiplexer #(.select(1), .width(4), .disabled("Z"), .enable("false")) multiplexer_1 (
    .in0(4'b0000), .in1(4'b1000), .out(multiplexer_1_out), .sel(or_1_out));
  Multiplexer #(.select(1), .width(4), .disabled("Z"), .enable("false")) multiplexer_2 (
    .in0(shifter_1_out[7:4]), .in1(subtractor_1_out), .out(multiplexer_2_out), .sel(or_1_out));
  or or_1 (or_1_out, comparator_1_gt, comparator_1_eq);
  Shifter #(.width(8), .shift("ll")) shifter_2 (
    .in({multiplexer_2_out, shifter_1_out[3:0]}), .\dist (3'b001), .out({shifter_2_out, shifter_2_out_2[3:0]}));
  Subtractor #(.width(4)) subtractor_2 (.a(shifter_2_out), .b(d), .out(subtractor_2_out));  // open: bin, bout
  Comparator #(.width(4), .mode("unsigned")) comparator_2 (
    .a(shifter_2_out), .b(d), .gt(comparator_2_gt), .eq(comparator_2_eq));  // open: lt
  Multiplexer #(.select(1), .width(4), .disabled("Z"), .enable("false")) multiplexer_3 (
    .in0(multiplexer_1_out), .in1({multiplexer_1_out[3], 1'b1, multiplexer_1_out[1:0]}),
    .out({multiplexer_3_out_2[3:2], multiplexer_3_out[1], multiplexer_3_out_2[0]}), .sel(or_2_out));
  Multiplexer #(.select(1), .width(4), .disabled("Z"), .enable("false")) multiplexer_4 (
    .in0(shifter_2_out), .in1(subtractor_2_out), .out(shifter_2_out_2[7:4]), .sel(or_2_out));
  or or_2 (or_2_out, comparator_2_gt, comparator_2_eq);
  Shifter #(.width(8), .shift("ll")) shifter_3 (.in(shifter_2_out_2), .\dist (3'b001), .out(shifter_3_out));
  Subtractor #(.width(4)) subtractor_3 (.a(shifter_3_out[7:4]), .b(d), .out(subtractor_3_out));  // open: bin, bout
  Comparator #(.width(4), .mode("unsigned")) comparator_3 (
    .a(shifter_3_out[7:4]), .b(d), .gt(comparator_3_gt), .eq(comparator_3_eq));  // open: lt
  Multiplexer #(.select(1), .width(4), .disabled("Z"), .enable("false")) multiplexer_5 (
    .in0({multiplexer_3_out_2[3:2], multiplexer_3_out[1], multiplexer_3_out_2[0]}),
    .in1({multiplexer_3_out_2[3:2], 1'b1, multiplexer_3_out_2[0]}), .out(multiplexer_5_out), .sel(or_3_out));
  Multiplexer #(.select(1), .width(4), .disabled("Z"), .enable("false")) multiplexer_6 (
    .in0(shifter_3_out[7:4]), .in1(subtractor_3_out), .out(multiplexer_6_out), .sel(or_3_out));
  or or_3 (or_3_out, comparator_3_gt, comparator_3_eq);
  Shifter #(.width(8), .shift("ll")) shifter_4 (
    .in({multiplexer_6_out, shifter_3_out[3:0]}), .\dist (3'b001), .out(shifter_4_out));
  Subtractor #(.width(4)) subtractor_4 (.a(shifter_4_out[7:4]), .b(d), .out(subtractor_4_out));  // open: bin, bout
  Comparator #(.width(4), .mode("unsigned")) comparator_4 (
    .a(shifter_4_out[7:4]), .b(d), .gt(comparator_4_gt), .eq(comparator_4_eq));  // open: lt
  or or_4 (or_4_out, comparator_4_gt, comparator_4_eq);
  Multiplexer #(.select(1), .width(4), .disabled("Z"), .enable("false")) multiplexer_7 (
    .in0(multiplexer_5_out), .in1({multiplexer_5_out[3:1], 1'b1}), .out(quot), .sel(or_4_out));
  Multiplexer #(.select(1), .width(4), .disabled("Z"), .enable("false")) multiplexer_8 (
    .in0(shifter_4_out[7:4]), .in1(subtractor_4_out), .out(rem), .sel(or_4_out));
endmodule

module \四位除法器测试电路  (
  input  [3:0] n2,
  input  [3:0] d,
  output [3:0] quot,
  output [3:0] rem
);

  \四位除法器  \u_四位除法器_1  (.n2(n2), .d(d), .quot(quot), .rem(rem));
endmodule

module \_32位除法器  (
  input  [31:0] n2,
  input  [31:0] d,
  output [31:0] quot,
  output [31:0] rem
);

  wire comparator_1_eq, comparator_1_gt, comparator_2_eq, comparator_2_gt, comparator_3_eq, comparator_3_gt,
       comparator_4_eq, comparator_4_gt, comparator_5_eq, comparator_5_gt, comparator_6_eq, comparator_6_gt,
       comparator_7_eq, comparator_7_gt, comparator_8_eq, comparator_8_gt, comparator_9_eq, comparator_9_gt,
       comparator_10_eq, comparator_10_gt, comparator_11_eq, comparator_11_gt, comparator_12_eq,
       comparator_12_gt, comparator_13_eq, comparator_13_gt, comparator_14_eq, comparator_14_gt,
       comparator_15_eq, comparator_15_gt, comparator_16_eq, comparator_16_gt, comparator_17_eq,
       comparator_17_gt, comparator_18_eq, comparator_18_gt, comparator_19_eq, comparator_19_gt,
       comparator_20_eq, comparator_20_gt, comparator_21_eq, comparator_21_gt, comparator_22_eq,
       comparator_22_gt, comparator_23_eq, comparator_23_gt, comparator_24_eq, comparator_24_gt,
       comparator_25_eq, comparator_25_gt, comparator_26_eq, comparator_26_gt, comparator_27_eq,
       comparator_27_gt, comparator_28_eq, comparator_28_gt, comparator_29_eq, comparator_29_gt,
       comparator_30_eq, comparator_30_gt, comparator_31_eq, comparator_31_gt, comparator_32_eq,
       comparator_32_gt, or_1_out, or_2_out, or_3_out, or_4_out, or_5_out, or_6_out, or_7_out, or_8_out,
       or_9_out, or_10_out, or_11_out, or_12_out, or_13_out, or_14_out, or_15_out, or_16_out, or_17_out,
       or_18_out, or_19_out, or_20_out, or_21_out, or_22_out, or_23_out, or_24_out, or_25_out, or_26_out,
       or_27_out, or_28_out, or_29_out, or_30_out, or_31_out, or_32_out;
  wire [0:0] multiplexer_61_out_2, shifter_15_out;
  wire [1:1] multiplexer_59_out_2;
  wire [2:2] multiplexer_57_out_2;
  wire [4:4] multiplexer_53_out_2;
  wire [5:5] multiplexer_51_out_2;
  wire [6:6] multiplexer_49_out_2;
  wire [8:8] multiplexer_45_out_2;
  wire [9:9] multiplexer_43_out_2;
  wire [10:10] multiplexer_41_out_2;
  wire [11:11] multiplexer_39_out_2;
  wire [12:12] multiplexer_37_out_2;
  wire [13:13] multiplexer_35_out_2;
  wire [16:16] multiplexer_29_out_2;
  wire [17:17] multiplexer_27_out_2;
  wire [18:18] multiplexer_25_out_2;
  wire [19:19] multiplexer_23_out_2;
  wire [20:20] multiplexer_21_out_2;
  wire [24:24] multiplexer_13_out;
  wire [26:26] multiplexer_9_out;
  wire [27:27] multiplexer_7_out;
  wire [28:28] multiplexer_5_out_2;
  wire [29:29] multiplexer_3_out_2;
  wire [30:0] shifter_15_out_2;
  wire [30:30] multiplexer_1_out;
  wire [31:0] multiplexer_1_out_2, multiplexer_2_out, multiplexer_3_out, multiplexer_4_out,
       multiplexer_5_out, multiplexer_6_out, multiplexer_7_out_2, multiplexer_8_out, multiplexer_9_out_2,
       multiplexer_10_out, multiplexer_11_out, multiplexer_12_out, multiplexer_13_out_2, multiplexer_14_out,
       multiplexer_15_out, multiplexer_16_out, multiplexer_17_out, multiplexer_18_out, multiplexer_19_out,
       multiplexer_20_out, multiplexer_21_out, multiplexer_22_out, multiplexer_23_out, multiplexer_25_out,
       multiplexer_27_out, multiplexer_29_out, multiplexer_30_out, multiplexer_31_out, multiplexer_32_out,
       multiplexer_33_out, multiplexer_35_out, multiplexer_36_out, multiplexer_37_out, multiplexer_39_out,
       multiplexer_40_out, multiplexer_41_out, multiplexer_43_out, multiplexer_45_out, multiplexer_47_out,
       multiplexer_48_out, multiplexer_49_out, multiplexer_51_out, multiplexer_53_out, multiplexer_55_out,
       multiplexer_57_out, multiplexer_59_out, multiplexer_60_out, shifter_1_out, shifter_2_out,
       shifter_3_out, shifter_4_out, shifter_5_out, shifter_6_out, shifter_7_out, shifter_8_out,
       shifter_9_out, shifter_10_out, shifter_11_out, shifter_12_out, shifter_13_out, shifter_14_out,
       shifter_16_out, shifter_17_out, shifter_18_out, shifter_19_out, shifter_20_out, shifter_21_out,
       shifter_22_out, shifter_23_out, shifter_24_out, shifter_25_out, shifter_26_out, shifter_27_out,
       shifter_28_out, shifter_29_out, shifter_30_out, shifter_31_out, subtractor_1_out, subtractor_2_out,
       subtractor_3_out, subtractor_4_out, subtractor_5_out, subtractor_6_out, subtractor_7_out,
       subtractor_8_out, subtractor_9_out, subtractor_10_out, subtractor_11_out, subtractor_12_out,
       subtractor_13_out, subtractor_14_out, subtractor_15_out, subtractor_16_out, subtractor_17_out,
       subtractor_18_out, subtractor_19_out, subtractor_20_out, subtractor_21_out, subtractor_22_out,
       subtractor_23_out, subtractor_24_out, subtractor_25_out, subtractor_26_out, subtractor_27_out,
       subtractor_28_out, subtractor_29_out, subtractor_30_out, subtractor_31_out, subtractor_32_out;
  wire [31:1] multiplexer_24_out, multiplexer_26_out, multiplexer_28_out, multiplexer_34_out,
       multiplexer_38_out, multiplexer_42_out, multiplexer_44_out, multiplexer_46_out, multiplexer_50_out,
       multiplexer_52_out, multiplexer_54_out, multiplexer_56_out, multiplexer_58_out, multiplexer_61_out,
       multiplexer_62_out;
  wire [31:31] multiplexer_24_out_2, multiplexer_26_out_2, multiplexer_28_out_2, multiplexer_34_out_2,
       multiplexer_38_out_2, multiplexer_42_out_2, multiplexer_44_out_2, multiplexer_46_out_2,
       multiplexer_50_out_2, multiplexer_52_out_2, multiplexer_54_out_2, multiplexer_56_out_2,
       multiplexer_58_out_2, multiplexer_62_out_2;

  Shifter #(.width(32), .shift("ll")) shifter_1 (.in(n2), .\dist (5'b00001), .out(shifter_1_out));
  Shifter #(.width(32), .shift("ll")) shifter_2 (.in(shifter_1_out), .\dist (5'b00001), .out(shifter_2_out));
  Shifter #(.width(32), .shift("ll")) shifter_3 (.in(shifter_2_out), .\dist (5'b00001), .out(shifter_3_out));
  Shifter #(.width(32), .shift("ll")) shifter_4 (.in(shifter_3_out), .\dist (5'b00001), .out(shifter_4_out));
  Shifter #(.width(32), .shift("ll")) shifter_5 (.in(shifter_4_out), .\dist (5'b00001), .out(shifter_5_out));
  Shifter #(.width(32), .shift("ll")) shifter_6 (.in(shifter_5_out), .\dist (5'b00001), .out(shifter_6_out));
  Shifter #(.width(32), .shift("ll")) shifter_7 (.in(shifter_6_out), .\dist (5'b00001), .out(shifter_7_out));
  Subtractor #(.width(32)) subtractor_1 (.a({{31{1'b0}}, n2[31]}), .b(d), .out(subtractor_1_out));  // open: bin, bout
  Comparator #(.width(32), .mode("twosComplement")) comparator_1 (
    .a({{31{1'b0}}, n2[31]}), .b(d), .gt(comparator_1_gt), .eq(comparator_1_eq));  // open: lt
  Multiplexer #(.select(1), .width(32), .disabled("Z"), .enable("false")) multiplexer_1 (
    .in0({32{1'b0}}), .in1(32'h80000000),
    .out({multiplexer_1_out_2[31], multiplexer_1_out[30], multiplexer_1_out_2[29:0]}), .sel(or_1_out));
  or or_1 (or_1_out, comparator_1_gt, comparator_1_eq);
  Multiplexer #(.select(1), .width(32), .disabled("Z"), .enable("false")) multiplexer_2 (
    .in0({{31{1'b0}}, n2[31]}), .in1(subtractor_1_out), .out(multiplexer_2_out), .sel(or_1_out));
  Subtractor #(.width(32)) subtractor_2 (
    .a({multiplexer_2_out[30:0], shifter_1_out[31]}), .b(d), .out(subtractor_2_out));  // open: bin, bout
  Comparator #(.width(32), .mode("twosComplement")) comparator_2 (
    .a({multiplexer_2_out[30:0], shifter_1_out[31]}), .b(d), .gt(comparator_2_gt), .eq(comparator_2_eq));  // open: lt
  Subtractor #(.width(32)) subtractor_3 (
    .a({multiplexer_4_out[30:0], shifter_2_out[31]}), .b(d), .out(subtractor_3_out));  // open: bin, bout
  Comparator #(.width(32), .mode("twosComplement")) comparator_3 (
    .a({multiplexer_4_out[30:0], shifter_2_out[31]}), .b(d), .gt(comparator_3_gt), .eq(comparator_3_eq));  // open: lt
  Subtractor #(.width(32)) subtractor_4 (
    .a({multiplexer_6_out[30:0], shifter_3_out[31]}), .b(d), .out(subtractor_4_out));  // open: bin, bout
  Comparator #(.width(32), .mode("twosComplement")) comparator_4 (
    .a({multiplexer_6_out[30:0], shifter_3_out[31]}), .b(d), .gt(comparator_4_gt), .eq(comparator_4_eq));  // open: lt
  Subtractor #(.width(32)) subtractor_5 (
    .a({multiplexer_8_out[30:0], shifter_4_out[31]}), .b(d), .out(subtractor_5_out));  // open: bin, bout
  Comparator #(.width(32), .mode("twosComplement")) comparator_5 (
    .a({multiplexer_8_out[30:0], shifter_4_out[31]}), .b(d), .gt(comparator_5_gt), .eq(comparator_5_eq));  // open: lt
  Subtractor #(.width(32)) subtractor_6 (
    .a({multiplexer_10_out[30:0], shifter_5_out[31]}), .b(d), .out(subtractor_6_out));  // open: bin, bout
  Comparator #(.width(32), .mode("twosComplement")) comparator_6 (
    .a({multiplexer_10_out[30:0], shifter_5_out[31]}), .b(d), .gt(comparator_6_gt), .eq(comparator_6_eq));  // open: lt
  Subtractor #(.width(32)) subtractor_7 (
    .a({multiplexer_12_out[30:0], shifter_6_out[31]}), .b(d), .out(subtractor_7_out));  // open: bin, bout
  Comparator #(.width(32), .mode("twosComplement")) comparator_7 (
    .a({multiplexer_12_out[30:0], shifter_6_out[31]}), .b(d), .gt(comparator_7_gt), .eq(comparator_7_eq));  // open: lt
  Subtractor #(.width(32)) subtractor_8 (
    .a({multiplexer_14_out[30:0], shifter_7_out[31]}), .b(d), .out(subtractor_8_out));  // open: bin, bout
  Comparator #(.width(32), .mode("twosComplement")) comparator_8 (
    .a({multiplexer_14_out[30:0], shifter_7_out[31]}), .b(d), .gt(comparator_8_gt), .eq(comparator_8_eq));  // open: lt
  Multiplexer #(.select(1), .width(32), .disabled("Z"), .enable("false")) multiplexer_3 (
    .in0({multiplexer_1_out_2[31], multiplexer_1_out[30], multiplexer_1_out_2[29:0]}),
    .in1({multiplexer_1_out_2[31], 1'b1, multiplexer_1_out_2[29:0]}),
    .out({multiplexer_3_out[31:30], multiplexer_3_out_2[29], multiplexer_3_out[28:0]}), .sel(or_2_out));
  Multiplexer #(.select(1), .width(32), .disabled("Z"), .enable("false")) multiplexer_4 (
    .in0({multiplexer_2_out[30:0], shifter_1_out[31]}), .in1(subtractor_2_out), .out(multiplexer_4_out),
    .sel(or_2_out));
  or or_2 (or_2_out, comparator_2_gt, comparator_2_eq);
  Multiplexer #(.select(1), .width(32), .disabled("Z"), .enable("false")) multiplexer_5 (
    .in0({multiplexer_3_out[31:30], multiplexer_3_out_2[29], multiplexer_3_out[28:0]}),
    .in1({multiplexer_3_out[31:30], 1'b1, multiplexer_3_out[28:0]}),
    .out({multiplexer_5_out[31:29], multiplexer_5_out_2[28], multiplexer_5_out[27:0]}), .sel(or_3_out));
  Multiplexer #(.select(1), .width(32), .disabled("Z"), .enable("false")) multiplexer_6 (
    .in0({multiplexer_4_out[30:0], shifter_2_out[31]}), .in1(subtractor_3_out), .out(multiplexer_6_out),
    .sel(or_3_out));
  or or_3 (or_3_out, comparator_3_gt, comparator_3_eq);
  Multiplexer #(.select(1), .width(32), .disabled("Z"), .enable("false")) multiplexer_7 (
    .in0({multiplexer_5_out[31:29], multiplexer_5_out_2[28], multiplexer_5_out[27:0]}),
    .in1({multiplexer_5_out[31:29], 1'b1, multiplexer_5_out[27:0]}),
    .out({multiplexer_7_out_2[31:28], multiplexer_7_out[27], multiplexer_7_out_2[26:0]}), .sel(or_4_out));
  Multiplexer #(.select(1), .width(32), .disabled("Z"), .enable("false")) multiplexer_8 (
    .in0({multiplexer_6_out[30:0], shifter_3_out[31]}), .in1(subtractor_4_out), .out(multiplexer_8_out),
    .sel(or_4_out));
  or or_4 (or_4_out, comparator_4_gt, comparator_4_eq);
  Multiplexer #(.select(1), .width(32), .disabled("Z"), .enable("false")) multiplexer_9 (
    .in0({multiplexer_7_out_2[31:28], multiplexer_7_out[27], multiplexer_7_out_2[26:0]}),
    .in1({multiplexer_7_out_2[31:28], 1'b1, multiplexer_7_out_2[26:0]}),
    .out({multiplexer_9_out_2[31:27], multiplexer_9_out[26], multiplexer_9_out_2[25:0]}), .sel(or_5_out));
  Multiplexer #(.select(1), .width(32), .disabled("Z"), .enable("false")) multiplexer_10 (
    .in0({multiplexer_8_out[30:0], shifter_4_out[31]}), .in1(subtractor_5_out), .out(multiplexer_10_out),
    .sel(or_5_out));
  or or_5 (or_5_out, comparator_5_gt, comparator_5_eq);
  Multiplexer #(.select(1), .width(32), .disabled("Z"), .enable("false")) multiplexer_11 (
    .in0({multiplexer_9_out_2[31:27], multiplexer_9_out[26], multiplexer_9_out_2[25:0]}),
    .in1({multiplexer_9_out_2[31:27], 1'b1, multiplexer_9_out_2[25:0]}), .out(multiplexer_11_out),
    .sel(or_6_out));
  Multiplexer #(.select(1), .width(32), .disabled("Z"), .enable("false")) multiplexer_12 (
    .in0({multiplexer_10_out[30:0], shifter_5_out[31]}), .in1(subtractor_6_out), .out(multiplexer_12_out),
    .sel(or_6_out));
  or or_6 (or_6_out, comparator_6_gt, comparator_6_eq);
  Multiplexer #(.select(1), .width(32), .disabled("Z"), .enable("false")) multiplexer_13 (
    .in0(multiplexer_11_out), .in1({multiplexer_11_out[31:26], 1'b1, multiplexer_11_out[24:0]}),
    .out({multiplexer_13_out_2[31:25], multiplexer_13_out[24], multiplexer_13_out_2[23:0]}), .sel(or_7_out));
  Multiplexer #(.select(1), .width(32), .disabled("Z"), .enable("false")) multiplexer_14 (
    .in0({multiplexer_12_out[30:0], shifter_6_out[31]}), .in1(subtractor_7_out), .out(multiplexer_14_out),
    .sel(or_7_out));
  or or_7 (or_7_out, comparator_7_gt, comparator_7_eq);
  Multiplexer #(.select(1), .width(32), .disabled("Z"), .enable("false")) multiplexer_15 (
    .in0({multiplexer_13_out_2[31:25], multiplexer_13_out[24], multiplexer_13_out_2[23:0]}),
    .in1({multiplexer_13_out_2[31:25], 1'b1, multiplexer_13_out_2[23:0]}), .out(multiplexer_15_out),
    .sel(or_8_out));
  Multiplexer #(.select(1), .width(32), .disabled("Z"), .enable("false")) multiplexer_16 (
    .in0({multiplexer_14_out[30:0], shifter_7_out[31]}), .in1(subtractor_8_out), .out(multiplexer_16_out),
    .sel(or_8_out));
  or or_8 (or_8_out, comparator_8_gt, comparator_8_eq);
  Shifter #(.width(32), .shift("ll")) shifter_8 (.in(shifter_7_out), .\dist (5'b00001), .out(shifter_8_out));
  Shifter #(.width(32), .shift("ll")) shifter_9 (.in(shifter_8_out), .\dist (5'b00001), .out(shifter_9_out));
  Shifter #(.width(32), .shift("ll")) shifter_10 (.in(shifter_9_out), .\dist (5'b00001), .out(shifter_10_out));
  Shifter #(.width(32), .shift("ll")) shifter_11 (.in(shifter_10_out), .\dist (5'b00001), .out(shifter_11_out));
  Shifter #(.width(32), .shift("ll")) shifter_12 (.in(shifter_11_out), .\dist (5'b00001), .out(shifter_12_out));
  Shifter #(.width(32), .shift("ll")) shifter_13 (.in(shifter_12_out), .\dist (5'b00001), .out(shifter_13_out));
  Shifter #(.width(32), .shift("ll")) shifter_14 (.in(shifter_13_out), .\dist (5'b00001), .out(shifter_14_out));
  Shifter #(.width(32), .shift("ll")) shifter_15 (
    .in(shifter_14_out), .\dist (5'b00001), .out({shifter_15_out[0], shifter_15_out_2}));
  Subtractor #(.width(32)) subtractor_9 (
    .a({multiplexer_18_out[30:0], shifter_9_out[31]}), .b(d), .out(subtractor_9_out));  // open: bin, bout
  Comparator #(.width(32), .mode("twosComplement")) comparator_9 (
    .a({multiplexer_18_out[30:0], shifter_9_out[31]}), .b(d), .gt(comparator_9_gt), .eq(comparator_9_eq));  // open: lt
  Subtractor #(.width(32)) subtractor_10 (
    .a({multiplexer_20_out[30:0], shifter_10_out[31]}), .b(d), .out(subtractor_10_out));  // open: bin, bout
  Comparator #(.width(32), .mode("twosComplement")) comparator_10 (
    .a({multiplexer_20_out[30:0], shifter_10_out[31]}), .b(d), .gt(comparator_10_gt), .eq(comparator_10_eq));  // open: lt
  Subtractor #(.width(32)) subtractor_11 (
    .a({multiplexer_22_out[30:0], shifter_11_out[31]}), .b(d), .out(subtractor_11_out));  // open: bin, bout
  Comparator #(.width(32), .mode("twosComplement")) comparator_11 (
    .a({multiplexer_22_out[30:0], shifter_11_out[31]}), .b(d), .gt(comparator_11_gt), .eq(comparator_11_eq));  // open: lt
  Subtractor #(.width(32)) subtractor_12 (
    .a({multiplexer_24_out, shifter_12_out[31]}), .b(d), .out(subtractor_12_out));  // open: bin, bout
  Comparator #(.width(32), .mode("twosComplement")) comparator_12 (
    .a({multiplexer_24_out, shifter_12_out[31]}), .b(d), .gt(comparator_12_gt), .eq(comparator_12_eq));  // open: lt
  Subtractor #(.width(32)) subtractor_13 (
    .a({multiplexer_16_out[30:0], shifter_8_out[31]}), .b(d), .out(subtractor_13_out));  // open: bin, bout
  or or_9 (or_9_out, comparator_13_gt, comparator_13_eq);
  Comparator #(.width(32), .mode("twosComplement")) comparator_13 (
    .a({multiplexer_16_out[30:0], shifter_8_out[31]}), .b(d), .gt(comparator_13_gt), .eq(comparator_13_eq));  // open: lt
  or or_10 (or_10_out, comparator_9_gt, comparator_9_eq);
  or or_11 (or_11_out, comparator_10_gt, comparator_10_eq);
  or or_12 (or_12_out, comparator_11_gt, comparator_11_eq);
  or or_13 (or_13_out, comparator_12_gt, comparator_12_eq);
  Subtractor #(.width(32)) subtractor_14 (
    .a({multiplexer_26_out, shifter_13_out[31]}), .b(d), .out(subtractor_14_out));  // open: bin, bout
  or or_14 (or_14_out, comparator_14_gt, comparator_14_eq);
  Comparator #(.width(32), .mode("twosComplement")) comparator_14 (
    .a({multiplexer_26_out, shifter_13_out[31]}), .b(d), .gt(comparator_14_gt), .eq(comparator_14_eq));  // open: lt
  Subtractor #(.width(32)) subtractor_15 (
    .a({multiplexer_28_out[31:24], {2{multiplexer_28_out[24]}}, multiplexer_28_out[21:1], shifter_14_out[31]}),
    .b(d), .out(subtractor_15_out));  // open: bin, bout
  Comparator #(.width(32), .mode("twosComplement")) comparator_15 (
    .a({multiplexer_28_out[31:24], {2{multiplexer_28_out[24]}}, multiplexer_28_out[21:1], shifter_14_out[31]}),
    .b(d), .gt(comparator_15_gt), .eq(comparator_15_eq));  // open: lt
  or or_15 (or_15_out, comparator_15_gt, comparator_15_eq);
  Subtractor #(.width(32)) subtractor_16 (
    .a({multiplexer_30_out[30:0], shifter_15_out[0]}), .b(d), .out(subtractor_16_out));  // open: bin, bout
  or or_16 (or_16_out, comparator_16_gt, comparator_16_eq);
  Comparator #(.width(32), .mode("twosComplement")) comparator_16 (
    .a({multiplexer_30_out[30:0], shifter_15_out[0]}), .b(d), .gt(comparator_16_gt), .eq(comparator_16_eq));  // open: lt
  Multiplexer #(.select(1), .width(32), .disabled("Z"), .enable("false")) multiplexer_17 (
    .in0(multiplexer_15_out), .in1({multiplexer_15_out[31:24], 1'b1, multiplexer_15_out[22:0]}),
    .out(multiplexer_17_out), .sel(or_9_out));
  Multiplexer #(.select(1), .width(32), .disabled("Z"), .enable("false")) multiplexer_18 (
    .in0({multiplexer_16_out[30:0], shifter_8_out[31]}), .in1(subtractor_13_out), .out(multiplexer_18_out),
    .sel(or_9_out));
  Multiplexer #(.select(1), .width(32), .disabled("Z"), .enable("false")) multiplexer_19 (
    .in0(multiplexer_17_out), .in1({multiplexer_17_out[31:23], 1'b1, multiplexer_17_out[21:0]}),
    .out(multiplexer_19_out), .sel(or_10_out));
  Multiplexer #(.select(1), .width(32), .disabled("Z"), .enable("false")) multiplexer_20 (
    .in0({multiplexer_18_out[30:0], shifter_9_out[31]}), .in1(subtractor_9_out), .out(multiplexer_20_out),
    .sel(or_10_out));
  Multiplexer #(.select(1), .width(32), .disabled("Z"), .enable("false")) multiplexer_21 (
    .in0(multiplexer_19_out), .in1({multiplexer_19_out[31:22], 1'b1, multiplexer_19_out[20:0]}),
    .out({multiplexer_21_out[31:21], multiplexer_21_out_2[20], multiplexer_21_out[19:0]}), .sel(or_11_out));
  Multiplexer #(.select(1), .width(32), .disabled("Z"), .enable("false")) multiplexer_22 (
    .in0({multiplexer_20_out[30:0], shifter_10_out[31]}), .in1(subtractor_10_out), .out(multiplexer_22_out),
    .sel(or_11_out));
  Multiplexer #(.select(1), .width(32), .disabled("Z"), .enable("false")) multiplexer_23 (
    .in0({multiplexer_21_out[31:21], multiplexer_21_out_2[20], multiplexer_21_out[19:0]}),
    .in1({multiplexer_21_out[31:21], 1'b1, multiplexer_21_out[19:0]}),
    .out({multiplexer_23_out[31:20], multiplexer_23_out_2[19], multiplexer_23_out[18:0]}), .sel(or_12_out));
  Multiplexer #(.select(1), .width(32), .disabled("Z"), .enable("false")) multiplexer_24 (
    .in0({multiplexer_22_out[30:0], shifter_11_out[31]}), .in1(subtractor_11_out),
    .out({multiplexer_24_out_2[31], multiplexer_24_out}), .sel(or_12_out));
  Multiplexer #(.select(1), .width(32), .disabled("Z"), .enable("false")) multiplexer_25 (
    .in0({multiplexer_23_out[31:20], multiplexer_23_out_2[19], multiplexer_23_out[18:0]}),
    .in1({multiplexer_23_out[31:20], 1'b1, multiplexer_23_out[18:0]}),
    .out({multiplexer_25_out[31:19], multiplexer_25_out_2[18], multiplexer_25_out[17:0]}), .sel(or_13_out));
  Multiplexer #(.select(1), .width(32), .disabled("Z"), .enable("false")) multiplexer_26 (
    .in0({multiplexer_24_out, shifter_12_out[31]}), .in1(subtractor_12_out),
    .out({multiplexer_26_out_2[31], multiplexer_26_out}), .sel(or_13_out));
  Multiplexer #(.select(1), .width(32), .disabled("Z"), .enable("false")) multiplexer_27 (
    .in0({multiplexer_25_out[31:19], multiplexer_25_out_2[18], multiplexer_25_out[17:0]}),
    .in1({multiplexer_25_out[31:19], 1'b1, multiplexer_25_out[17:0]}),
    .out({multiplexer_27_out[31:18], multiplexer_27_out_2[17], multiplexer_27_out[16:0]}), .sel(or_14_out));
  Multiplexer #(.select(1), .width(32), .disabled("Z"), .enable("false")) multiplexer_28 (
    .in0({multiplexer_26_out, shifter_13_out[31]}), .in1(subtractor_14_out),
    .out({multiplexer_28_out_2[31], multiplexer_28_out[31:24], {2{multiplexer_28_out[24]}}, multiplexer_28_out[21:1]}),
    .sel(or_14_out));
  Multiplexer #(.select(1), .width(32), .disabled("Z"), .enable("false")) multiplexer_29 (
    .in0({multiplexer_27_out[31:18], multiplexer_27_out_2[17], multiplexer_27_out[16:0]}),
    .in1({multiplexer_27_out[31:18], 1'b1, multiplexer_27_out[16:0]}),
    .out({multiplexer_29_out[31:17], multiplexer_29_out_2[16], multiplexer_29_out[15:0]}), .sel(or_15_out));
  Multiplexer #(.select(1), .width(32), .disabled("Z"), .enable("false")) multiplexer_30 (
    .in0({multiplexer_28_out[31:24], {2{multiplexer_28_out[24]}}, multiplexer_28_out[21:1], shifter_14_out[31]}),
    .in1(subtractor_15_out), .out(multiplexer_30_out), .sel(or_15_out));
  Multiplexer #(.select(1), .width(32), .disabled("Z"), .enable("false")) multiplexer_31 (
    .in0({multiplexer_29_out[31:17], multiplexer_29_out_2[16], multiplexer_29_out[15:0]}),
    .in1({multiplexer_29_out[31:17], 1'b1, multiplexer_29_out[15:0]}), .out(multiplexer_31_out),
    .sel(or_16_out));
  Multiplexer #(.select(1), .width(32), .disabled("Z"), .enable("false")) multiplexer_32 (
    .in0({multiplexer_30_out[30:0], shifter_15_out[0]}), .in1(subtractor_16_out), .out(multiplexer_32_out),
    .sel(or_16_out));
  Shifter #(.width(32), .shift("ll")) shifter_16 (
    .in({shifter_15_out[0], shifter_15_out_2}), .\dist (5'b00001), .out(shifter_16_out));
  Shifter #(.width(32), .shift("ll")) shifter_17 (.in(shifter_16_out), .\dist (5'b00001), .out(shifter_17_out));
  Shifter #(.width(32), .shift("ll")) shifter_18 (.in(shifter_17_out), .\dist (5'b00001), .out(shifter_18_out));
  Shifter #(.width(32), .shift("ll")) shifter_19 (.in(shifter_18_out), .\dist (5'b00001), .out(shifter_19_out));
  Shifter #(.width(32), .shift("ll")) shifter_20 (.in(shifter_19_out), .\dist (5'b00001), .out(shifter_20_out));
  Shifter #(.width(32), .shift("ll")) shifter_21 (.in(shifter_20_out), .\dist (5'b00001), .out(shifter_21_out));
  Shifter #(.width(32), .shift("ll")) shifter_22 (.in(shifter_21_out), .\dist (5'b00001), .out(shifter_22_out));
  Shifter #(.width(32), .shift("ll")) shifter_23 (.in(shifter_22_out), .\dist (5'b00001), .out(shifter_23_out));
  Subtractor #(.width(32)) subtractor_17 (
    .a({multiplexer_32_out[30:0], shifter_16_out[31]}), .b(d), .out(subtractor_17_out));  // open: bin, bout
  Comparator #(.width(32), .mode("twosComplement")) comparator_17 (
    .a({multiplexer_32_out[30:0], shifter_16_out[31]}), .b(d), .gt(comparator_17_gt), .eq(comparator_17_eq));  // open: lt
  Subtractor #(.width(32)) subtractor_18 (
    .a({multiplexer_34_out, shifter_17_out[31]}), .b(d), .out(subtractor_18_out));  // open: bin, bout
  Comparator #(.width(32), .mode("twosComplement")) comparator_18 (
    .a({multiplexer_34_out, shifter_17_out[31]}), .b(d), .gt(comparator_18_gt), .eq(comparator_18_eq));  // open: lt
  Subtractor #(.width(32)) subtractor_19 (
    .a({multiplexer_36_out[30:0], shifter_18_out[31]}), .b(d), .out(subtractor_19_out));  // open: bin, bout
  Comparator #(.width(32), .mode("twosComplement")) comparator_19 (
    .a({multiplexer_36_out[30:0], shifter_18_out[31]}), .b(d), .gt(comparator_19_gt), .eq(comparator_19_eq));  // open: lt
  Subtractor #(.width(32)) subtractor_20 (
    .a({multiplexer_38_out, shifter_19_out[31]}), .b(d), .out(subtractor_20_out));  // open: bin, bout
  Comparator #(.width(32), .mode("twosComplement")) comparator_20 (
    .a({multiplexer_38_out, shifter_19_out[31]}), .b(d), .gt(comparator_20_gt), .eq(comparator_20_eq));  // open: lt
  Subtractor #(.width(32)) subtractor_21 (
    .a({multiplexer_40_out[30:0], shifter_20_out[31]}), .b(d), .out(subtractor_21_out));  // open: bin, bout
  Comparator #(.width(32), .mode("twosComplement")) comparator_21 (
    .a({multiplexer_40_out[30:0], shifter_20_out[31]}), .b(d), .gt(comparator_21_gt), .eq(comparator_21_eq));  // open: lt
  Subtractor #(.width(32)) subtractor_22 (
    .a({multiplexer_42_out, shifter_21_out[31]}), .b(d), .out(subtractor_22_out));  // open: bin, bout
  Comparator #(.width(32), .mode("twosComplement")) comparator_22 (
    .a({multiplexer_42_out, shifter_21_out[31]}), .b(d), .gt(comparator_22_gt), .eq(comparator_22_eq));  // open: lt
  Subtractor #(.width(32)) subtractor_23 (
    .a({multiplexer_44_out, shifter_22_out[31]}), .b(d), .out(subtractor_23_out));  // open: bin, bout
  Comparator #(.width(32), .mode("twosComplement")) comparator_23 (
    .a({multiplexer_44_out, shifter_22_out[31]}), .b(d), .gt(comparator_23_gt), .eq(comparator_23_eq));  // open: lt
  Subtractor #(.width(32)) subtractor_24 (
    .a({multiplexer_46_out, shifter_23_out[31]}), .b(d), .out(subtractor_24_out));  // open: bin, bout
  Comparator #(.width(32), .mode("twosComplement")) comparator_24 (
    .a({multiplexer_46_out, shifter_23_out[31]}), .b(d), .gt(comparator_24_gt), .eq(comparator_24_eq));  // open: lt
  or or_17 (or_17_out, comparator_17_gt, comparator_17_eq);
  or or_18 (or_18_out, comparator_18_gt, comparator_18_eq);
  or or_19 (or_19_out, comparator_19_gt, comparator_19_eq);
  or or_20 (or_20_out, comparator_20_gt, comparator_20_eq);
  or or_21 (or_21_out, comparator_21_gt, comparator_21_eq);
  or or_22 (or_22_out, comparator_22_gt, comparator_22_eq);
  or or_23 (or_23_out, comparator_23_gt, comparator_23_eq);
  or or_24 (or_24_out, comparator_24_gt, comparator_24_eq);
  Multiplexer #(.select(1), .width(32), .disabled("Z"), .enable("false")) multiplexer_33 (
    .in0(multiplexer_31_out), .in1({multiplexer_31_out[31:16], 1'b1, multiplexer_31_out[14:0]}),
    .out(multiplexer_33_out), .sel(or_17_out));
  Multiplexer #(.select(1), .width(32), .disabled("Z"), .enable("false")) multiplexer_34 (
    .in0({multiplexer_32_out[30:0], shifter_16_out[31]}), .in1(subtractor_17_out),
    .out({multiplexer_34_out_2[31], multiplexer_34_out}), .sel(or_17_out));
  Multiplexer #(.select(1), .width(32), .disabled("Z"), .enable("false")) multiplexer_35 (
    .in0(multiplexer_33_out), .in1({multiplexer_33_out[31:15], 1'b1, multiplexer_33_out[13:0]}),
    .out({multiplexer_35_out[31:14], multiplexer_35_out_2[13], multiplexer_35_out[12:0]}), .sel(or_18_out));
  Multiplexer #(.select(1), .width(32), .disabled("Z"), .enable("false")) multiplexer_36 (
    .in0({multiplexer_34_out, shifter_17_out[31]}), .in1(subtractor_18_out), .out(multiplexer_36_out),
    .sel(or_18_out));
  Multiplexer #(.select(1), .width(32), .disabled("Z"), .enable("false")) multiplexer_37 (
    .in0({multiplexer_35_out[31:14], multiplexer_35_out_2[13], multiplexer_35_out[12:0]}),
    .in1({multiplexer_35_out[31:14], 1'b1, multiplexer_35_out[12:0]}),
    .out({multiplexer_37_out[31:13], multiplexer_37_out_2[12], multiplexer_37_out[11:0]}), .sel(or_19_out));
  Multiplexer #(.select(1), .width(32), .disabled("Z"), .enable("false")) multiplexer_38 (
    .in0({multiplexer_36_out[30:0], shifter_18_out[31]}), .in1(subtractor_19_out),
    .out({multiplexer_38_out_2[31], multiplexer_38_out}), .sel(or_19_out));
  Multiplexer #(.select(1), .width(32), .disabled("Z"), .enable("false")) multiplexer_39 (
    .in0({multiplexer_37_out[31:13], multiplexer_37_out_2[12], multiplexer_37_out[11:0]}),
    .in1({multiplexer_37_out[31:13], 1'b1, multiplexer_37_out[11:0]}),
    .out({multiplexer_39_out[31:12], multiplexer_39_out_2[11], multiplexer_39_out[10:0]}), .sel(or_20_out));
  Multiplexer #(.select(1), .width(32), .disabled("Z"), .enable("false")) multiplexer_40 (
    .in0({multiplexer_38_out, shifter_19_out[31]}), .in1(subtractor_20_out), .out(multiplexer_40_out),
    .sel(or_20_out));
  Multiplexer #(.select(1), .width(32), .disabled("Z"), .enable("false")) multiplexer_41 (
    .in0({multiplexer_39_out[31:12], multiplexer_39_out_2[11], multiplexer_39_out[10:0]}),
    .in1({multiplexer_39_out[31:12], 1'b1, multiplexer_39_out[10:0]}),
    .out({multiplexer_41_out[31:11], multiplexer_41_out_2[10], multiplexer_41_out[9:0]}), .sel(or_21_out));
  Multiplexer #(.select(1), .width(32), .disabled("Z"), .enable("false")) multiplexer_42 (
    .in0({multiplexer_40_out[30:0], shifter_20_out[31]}), .in1(subtractor_21_out),
    .out({multiplexer_42_out_2[31], multiplexer_42_out}), .sel(or_21_out));
  Multiplexer #(.select(1), .width(32), .disabled("Z"), .enable("false")) multiplexer_43 (
    .in0({multiplexer_41_out[31:11], multiplexer_41_out_2[10], multiplexer_41_out[9:0]}),
    .in1({multiplexer_41_out[31:11], 1'b1, multiplexer_41_out[9:0]}),
    .out({multiplexer_43_out[31:10], multiplexer_43_out_2[9], multiplexer_43_out[8:0]}), .sel(or_22_out));
  Multiplexer #(.select(1), .width(32), .disabled("Z"), .enable("false")) multiplexer_44 (
    .in0({multiplexer_42_out, shifter_21_out[31]}), .in1(subtractor_22_out),
    .out({multiplexer_44_out_2[31], multiplexer_44_out}), .sel(or_22_out));
  Multiplexer #(.select(1), .width(32), .disabled("Z"), .enable("false")) multiplexer_45 (
    .in0({multiplexer_43_out[31:10], multiplexer_43_out_2[9], multiplexer_43_out[8:0]}),
    .in1({multiplexer_43_out[31:10], 1'b1, multiplexer_43_out[8:0]}),
    .out({multiplexer_45_out[31:9], multiplexer_45_out_2[8], multiplexer_45_out[7:0]}), .sel(or_23_out));
  Multiplexer #(.select(1), .width(32), .disabled("Z"), .enable("false")) multiplexer_46 (
    .in0({multiplexer_44_out, shifter_22_out[31]}), .in1(subtractor_23_out),
    .out({multiplexer_46_out_2[31], multiplexer_46_out}), .sel(or_23_out));
  Multiplexer #(.select(1), .width(32), .disabled("Z"), .enable("false")) multiplexer_47 (
    .in0({multiplexer_45_out[31:9], multiplexer_45_out_2[8], multiplexer_45_out[7:0]}),
    .in1({multiplexer_45_out[31:9], 1'b1, multiplexer_45_out[7:0]}), .out(multiplexer_47_out), .sel(or_24_out));
  Multiplexer #(.select(1), .width(32), .disabled("Z"), .enable("false")) multiplexer_48 (
    .in0({multiplexer_46_out, shifter_23_out[31]}), .in1(subtractor_24_out), .out(multiplexer_48_out),
    .sel(or_24_out));
  Shifter #(.width(32), .shift("ll")) shifter_24 (.in(shifter_23_out), .\dist (5'b00001), .out(shifter_24_out));
  Shifter #(.width(32), .shift("ll")) shifter_25 (.in(shifter_24_out), .\dist (5'b00001), .out(shifter_25_out));
  Shifter #(.width(32), .shift("ll")) shifter_26 (.in(shifter_25_out), .\dist (5'b00001), .out(shifter_26_out));
  Shifter #(.width(32), .shift("ll")) shifter_27 (.in(shifter_26_out), .\dist (5'b00001), .out(shifter_27_out));
  Shifter #(.width(32), .shift("ll")) shifter_28 (.in(shifter_27_out), .\dist (5'b00001), .out(shifter_28_out));
  Shifter #(.width(32), .shift("ll")) shifter_29 (.in(shifter_28_out), .\dist (5'b00001), .out(shifter_29_out));
  Shifter #(.width(32), .shift("ll")) shifter_30 (.in(shifter_29_out), .\dist (5'b00001), .out(shifter_30_out));
  Shifter #(.width(32), .shift("ll")) shifter_31 (.in(shifter_30_out), .\dist (5'b00001), .out(shifter_31_out));
  Subtractor #(.width(32)) subtractor_25 (
    .a({multiplexer_48_out[30:0], shifter_24_out[31]}), .b(d), .out(subtractor_25_out));  // open: bin, bout
  Comparator #(.width(32), .mode("twosComplement")) comparator_25 (
    .a({multiplexer_48_out[30:0], shifter_24_out[31]}), .b(d), .gt(comparator_25_gt), .eq(comparator_25_eq));  // open: lt
  Subtractor #(.width(32)) subtractor_26 (
    .a({multiplexer_50_out, shifter_25_out[31]}), .b(d), .out(subtractor_26_out));  // open: bin, bout
  Comparator #(.width(32), .mode("twosComplement")) comparator_26 (
    .a({multiplexer_50_out, shifter_25_out[31]}), .b(d), .gt(comparator_26_gt), .eq(comparator_26_eq));  // open: lt
  Subtractor #(.width(32)) subtractor_27 (
    .a({multiplexer_52_out, shifter_26_out[31]}), .b(d), .out(subtractor_27_out));  // open: bin, bout
  Comparator #(.width(32), .mode("twosComplement")) comparator_27 (
    .a({multiplexer_52_out, shifter_26_out[31]}), .b(d), .gt(comparator_27_gt), .eq(comparator_27_eq));  // open: lt
  Subtractor #(.width(32)) subtractor_28 (
    .a({multiplexer_54_out, shifter_27_out[31]}), .b(d), .out(subtractor_28_out));  // open: bin, bout
  Comparator #(.width(32), .mode("twosComplement")) comparator_28 (
    .a({multiplexer_54_out, shifter_27_out[31]}), .b(d), .gt(comparator_28_gt), .eq(comparator_28_eq));  // open: lt
  Subtractor #(.width(32)) subtractor_29 (
    .a({multiplexer_56_out, shifter_28_out[31]}), .b(d), .out(subtractor_29_out));  // open: bin, bout
  Comparator #(.width(32), .mode("twosComplement")) comparator_29 (
    .a({multiplexer_56_out, shifter_28_out[31]}), .b(d), .gt(comparator_29_gt), .eq(comparator_29_eq));  // open: lt
  Subtractor #(.width(32)) subtractor_30 (
    .a({multiplexer_58_out, shifter_29_out[31]}), .b(d), .out(subtractor_30_out));  // open: bin, bout
  Comparator #(.width(32), .mode("twosComplement")) comparator_30 (
    .a({multiplexer_58_out, shifter_29_out[31]}), .b(d), .gt(comparator_30_gt), .eq(comparator_30_eq));  // open: lt
  Subtractor #(.width(32)) subtractor_31 (
    .a({multiplexer_60_out[30:0], shifter_30_out[31]}), .b(d), .out(subtractor_31_out));  // open: bin, bout
  Comparator #(.width(32), .mode("twosComplement")) comparator_31 (
    .a({multiplexer_60_out[30:0], shifter_30_out[31]}), .b(d), .gt(comparator_31_gt), .eq(comparator_31_eq));  // open: lt
  Subtractor #(.width(32)) subtractor_32 (
    .a({multiplexer_62_out, shifter_31_out[31]}), .b(d), .out(subtractor_32_out));  // open: bin, bout
  Comparator #(.width(32), .mode("twosComplement")) comparator_32 (
    .a({multiplexer_62_out, shifter_31_out[31]}), .b(d), .gt(comparator_32_gt), .eq(comparator_32_eq));  // open: lt
  or or_25 (or_25_out, comparator_25_gt, comparator_25_eq);
  or or_26 (or_26_out, comparator_26_gt, comparator_26_eq);
  or or_27 (or_27_out, comparator_27_gt, comparator_27_eq);
  or or_28 (or_28_out, comparator_28_gt, comparator_28_eq);
  or or_29 (or_29_out, comparator_29_gt, comparator_29_eq);
  or or_30 (or_30_out, comparator_30_gt, comparator_30_eq);
  or or_31 (or_31_out, comparator_31_gt, comparator_31_eq);
  or or_32 (or_32_out, comparator_32_gt, comparator_32_eq);
  Multiplexer #(.select(1), .width(32), .disabled("Z"), .enable("false")) multiplexer_49 (
    .in0(multiplexer_47_out), .in1({multiplexer_47_out[31:8], 1'b1, multiplexer_47_out[6:0]}),
    .out({multiplexer_49_out[31:7], multiplexer_49_out_2[6], multiplexer_49_out[5:0]}), .sel(or_25_out));
  Multiplexer #(.select(1), .width(32), .disabled("Z"), .enable("false")) multiplexer_50 (
    .in0({multiplexer_48_out[30:0], shifter_24_out[31]}), .in1(subtractor_25_out),
    .out({multiplexer_50_out_2[31], multiplexer_50_out}), .sel(or_25_out));
  Multiplexer #(.select(1), .width(32), .disabled("Z"), .enable("false")) multiplexer_51 (
    .in0({multiplexer_49_out[31:7], multiplexer_49_out_2[6], multiplexer_49_out[5:0]}),
    .in1({multiplexer_49_out[31:7], 1'b1, multiplexer_49_out[5:0]}),
    .out({multiplexer_51_out[31:6], multiplexer_51_out_2[5], multiplexer_51_out[4:0]}), .sel(or_26_out));
  Multiplexer #(.select(1), .width(32), .disabled("Z"), .enable("false")) multiplexer_52 (
    .in0({multiplexer_50_out, shifter_25_out[31]}), .in1(subtractor_26_out),
    .out({multiplexer_52_out_2[31], multiplexer_52_out}), .sel(or_26_out));
  Multiplexer #(.select(1), .width(32), .disabled("Z"), .enable("false")) multiplexer_53 (
    .in0({multiplexer_51_out[31:6], multiplexer_51_out_2[5], multiplexer_51_out[4:0]}),
    .in1({multiplexer_51_out[31:6], 1'b1, multiplexer_51_out[4:0]}),
    .out({multiplexer_53_out[31:5], multiplexer_53_out_2[4], multiplexer_53_out[3:0]}), .sel(or_27_out));
  Multiplexer #(.select(1), .width(32), .disabled("Z"), .enable("false")) multiplexer_54 (
    .in0({multiplexer_52_out, shifter_26_out[31]}), .in1(subtractor_27_out),
    .out({multiplexer_54_out_2[31], multiplexer_54_out}), .sel(or_27_out));
  Multiplexer #(.select(1), .width(32), .disabled("Z"), .enable("false")) multiplexer_55 (
    .in0({multiplexer_53_out[31:5], multiplexer_53_out_2[4], multiplexer_53_out[3:0]}),
    .in1({multiplexer_53_out[31:5], 1'b1, multiplexer_53_out[3:0]}), .out(multiplexer_55_out), .sel(or_28_out));
  Multiplexer #(.select(1), .width(32), .disabled("Z"), .enable("false")) multiplexer_56 (
    .in0({multiplexer_54_out, shifter_27_out[31]}), .in1(subtractor_28_out),
    .out({multiplexer_56_out_2[31], multiplexer_56_out}), .sel(or_28_out));
  Multiplexer #(.select(1), .width(32), .disabled("Z"), .enable("false")) multiplexer_57 (
    .in0(multiplexer_55_out), .in1({multiplexer_55_out[31:4], 1'b1, multiplexer_55_out[2:0]}),
    .out({multiplexer_57_out[31:3], multiplexer_57_out_2[2], multiplexer_57_out[1:0]}), .sel(or_29_out));
  Multiplexer #(.select(1), .width(32), .disabled("Z"), .enable("false")) multiplexer_58 (
    .in0({multiplexer_56_out, shifter_28_out[31]}), .in1(subtractor_29_out),
    .out({multiplexer_58_out_2[31], multiplexer_58_out}), .sel(or_29_out));
  Multiplexer #(.select(1), .width(32), .disabled("Z"), .enable("false")) multiplexer_59 (
    .in0({multiplexer_57_out[31:3], multiplexer_57_out_2[2], multiplexer_57_out[1:0]}),
    .in1({multiplexer_57_out[31:3], 1'b1, multiplexer_57_out[1:0]}),
    .out({multiplexer_59_out[31:2], multiplexer_59_out_2[1], multiplexer_59_out[0]}), .sel(or_30_out));
  Multiplexer #(.select(1), .width(32), .disabled("Z"), .enable("false")) multiplexer_60 (
    .in0({multiplexer_58_out, shifter_29_out[31]}), .in1(subtractor_30_out), .out(multiplexer_60_out),
    .sel(or_30_out));
  Multiplexer #(.select(1), .width(32), .disabled("Z"), .enable("false")) multiplexer_61 (
    .in0({multiplexer_59_out[31:2], multiplexer_59_out_2[1], multiplexer_59_out[0]}),
    .in1({multiplexer_59_out[31:2], 1'b1, multiplexer_59_out[0]}),
    .out({multiplexer_61_out, multiplexer_61_out_2[0]}), .sel(or_31_out));
  Multiplexer #(.select(1), .width(32), .disabled("Z"), .enable("false")) multiplexer_62 (
    .in0({multiplexer_60_out[30:0], shifter_30_out[31]}), .in1(subtractor_31_out),
    .out({multiplexer_62_out_2[31], multiplexer_62_out}), .sel(or_31_out));
  Multiplexer #(.select(1), .width(32), .disabled("Z"), .enable("false")) multiplexer_63 (
    .in0({multiplexer_61_out, multiplexer_61_out_2[0]}), .in1({multiplexer_61_out, 1'b1}), .out(quot),
    .sel(or_32_out));
  Multiplexer #(.select(1), .width(32), .disabled("Z"), .enable("false")) multiplexer_64 (
    .in0({multiplexer_62_out, shifter_31_out[31]}), .in1(subtractor_32_out), .out(rem), .sel(or_32_out));
endmodule

module \_32位除法器测试电路  (
  input  [31:0] in_1,
  input  [31:0] in_2,
  output [31:0] out_3,
  output [31:0] out_4
);

  \_32位除法器  \u_32位除法器_1  (.n2(in_1), .d(in_2), .quot(out_3), .rem(out_4));
endmodule
