// Logisim project 实验5.circ as structural Verilog: 12 circuits, main circuit 四位二进制可逆计数器
module \四位二进制可逆计数器  (
  input  CPD,
  input  CPU,
  input  CLR,
  input  nLD,
  input  A,
  input  B,
  input  C,
  input  D,
  output QA,
  output QB,
  output QC,
  output QD
);

  wire and_1_out, and_2_out, and_3_out, and_4_out, and_5_out, and_6_out, and_7_out, and_8_out, and_9_out,
       and_10_out, and_11_out, and_12_out, and_13_out, and_14_out, and_15_out, d_ff_1_qn, d_ff_2_qn,
       d_ff_3_qn, d_ff_4_qn, not_1_out, not_2_out, not_3_out, not_4_out, not_5_out, or_1_out, or_2_out,
       or_3_out, or_4_out, or_5_out, or_6_out, or_7_out, or_8_out, or_9_out;

  and and_1 (and_1_out, or_9_out, CPD);
  or or_1 (or_1_out, and_1_out, CPU);
  and and_2 (and_2_out, d_ff_1_qn, and_1_out);
  and and_3 (and_3_out, QA, CPU);
  and and_4 (and_4_out, d_ff_1_qn, d_ff_2_qn, and_1_out);
  and and_5 (and_5_out, QA, QB, CPU);
  and and_6 (and_6_out, d_ff_1_qn, d_ff_2_qn, d_ff_3_qn, and_1_out);
  and and_7 (and_7_out, QA, QB, QC, CPU);
  not not_1 (not_1_out, nLD);
  not not_2 (not_2_out, A);
  not not_3 (not_3_out, B);
  not not_4 (not_4_out, C);
  not not_5 (not_5_out, D);
  or or_2 (or_2_out, and_2_out, and_3_out);
  or or_3 (or_3_out, and_4_out, and_5_out);
  or or_4 (or_4_out, and_6_out, and_7_out);
  and and_8 (and_8_out, not_1_out, A);
  and and_9 (and_9_out, not_1_out, not_2_out);
  and and_10 (and_10_out, not_1_out, B);
  and and_11 (and_11_out, not_1_out, not_3_out);
  and and_12 (and_12_out, not_1_out, C);
  and and_13 (and_13_out, not_1_out, not_4_out);
  and and_14 (and_14_out, not_1_out, D);
  and and_15 (and_15_out, not_1_out, not_5_out);
  or or_5 (or_5_out, and_9_out, CLR);
  or or_6 (or_6_out, and_11_out, CLR);
  or or_7 (or_7_out, and_13_out, CLR);
  or or_8 (or_8_out, and_15_out, CLR);
  D_Flip_Flop #(.trigger("falling"), .Pre_Clr_Positions("LEGACY"), .NegatePresetClear("false"), .enable("true"), .NewFFLayout("true")) d_ff_1 (
    .clk(or_1_out), .D(d_ff_1_qn), .Q(QA), .Qn(d_ff_1_qn), .preset(and_8_out), .en(nLD), .reset(or_5_out));
  D_Flip_Flop #(.trigger("falling"), .Pre_Clr_Positions("LEGACY"), .NegatePresetClear("false"), .enable("true"), .NewFFLayout("true")) d_ff_2 (
    .clk(or_2_out), .D(d_ff_2_qn), .Q(QB), .Qn(d_ff_2_qn), .preset(and_10_out), .en(nLD), .reset(or_6_out));
  D_Flip_Flop #(.trigger("falling"), .Pre_Clr_Positions("LEGACY"), .NegatePresetClear("false"), .enable("true"), .NewFFLayout("true")) d_ff_3 (
    .clk(or_3_out), .D(d_ff_3_qn), .Q(QC), .Qn(d_ff_3_qn), .preset(and_12_out), .en(nLD), .reset(or_7_out));
  D_Flip_Flop #(.trigger("falling"), .Pre_Clr_Positions("LEGACY"), .NegatePresetClear("false"), .enable("true"), .NewFFLayout("true")) d_ff_4 (
    .clk(or_4_out), .D(d_ff_4_qn), .Q(QD), .Qn(d_ff_4_qn), .preset(and_14_out), .en(nLD), .reset(or_8_out));
  or or_9 (or_9_out, QA, QB, QC, QD);
endmodule

module \六十进制计数器  (
  input  CPU,
  input  Clr,
  input  CPD,
  input  Adj,
  output out_5,
  output out_6,
  output out_7,
  output out_8,
  output out_9,
  output out_10,
  output out_11,
  output out_12,
  output out_13
);

  wire and_1_out, and_2_out, and_3_out, nand_1_out, nand_2_out, nor_1_out, nor_2_out, not_1_out, not_2_out,
       not_3_out, or_1_out, or_2_out;

  or or_1 (or_1_out, Clr, and_2_out);
  and and_1 (and_1_out, CPD, Adj, nand_2_out);
  \四位二进制可逆计数器  \u_四位二进制可逆计数器_1  (
    .CPD(and_1_out), .QA(out_8), .CPU(CPU), .QB(out_7), .QC(out_6), .QD(out_5), .CLR(or_1_out),
    .nLD(nand_1_out), .D(1'b1), .C(1'b0), .B(1'b0), .A(1'b1));
  nand nand_1 (nand_1_out, not_1_out, and_3_out);
  not not_1 (not_1_out, CPD);
  not not_2 (not_2_out, out_6);
  not not_3 (not_3_out, out_8);
  nor nor_1 (nor_1_out, out_5, out_6, out_7, out_8);
  and and_2 (and_2_out, out_5, not_2_out, out_7, not_3_out);
  nand nand_2 (nand_2_out, nor_1_out, nor_2_out);
  and and_3 (and_3_out, nor_1_out, and_1_out);
  or or_2 (or_2_out, out_9, Clr);
  and and_4 (out_9, out_11, out_12);
  \四位二进制可逆计数器  \u_四位二进制可逆计数器_2  (
    .CPD(and_3_out), .QA(out_13), .CPU(and_2_out), .QB(out_12), .QC(out_11), .QD(out_10), .CLR(or_2_out),
    .D(1'b0), .C(1'b0), .B(1'b0), .A(1'b0));  // open: nLD
  nor nor_2 (nor_2_out, out_10, out_11, out_12, out_13);
endmodule

module \六十进制计数器测试电路  (
  input  in_1,
  input  in_2
);

  wire button_1_out, button_2_out, \六十进制计数器_1_out_9 ;
  wire [3:0] \六十进制计数器_1_out_8 , \六十进制计数器_1_out_13 , \四位二进制可逆计数器_1_qa ;

  Button button_1 (.out(button_1_out));
  Button button_2 (.out(button_2_out));
  Hex_Digit_Display hex_digit_display_1 (.value(\六十进制计数器_1_out_13 ));  // open: dp
  \六十进制计数器  \u_六十进制计数器_1  (
    .CPU(button_1_out), .out_5(\六十进制计数器_1_out_8 [3]), .out_6(\六十进制计数器_1_out_8 [2]),
    .out_7(\六十进制计数器_1_out_8 [1]), .out_8(\六十进制计数器_1_out_8 [0]), .out_9(\六十进制计数器_1_out_9 ),
    .out_10(\六十进制计数器_1_out_13 [3]), .out_11(\六十进制计数器_1_out_13 [2]), .out_12(\六十进制计数器_1_out_13 [1]),
    .out_13(\六十进制计数器_1_out_13 [0]), .Clr(in_2), .CPD(button_2_out), .Adj(in_1));
  Hex_Digit_Display hex_digit_display_2 (.value(\六十进制计数器_1_out_8 ));  // open: dp
  Hex_Digit_Display hex_digit_display_3 (.value(\四位二进制可逆计数器_1_qa ));  // open: dp
  \四位二进制可逆计数器  \u_四位二进制可逆计数器_1  (
    .CPD(1'b0), .QA(\四位二进制可逆计数器_1_qa [0]), .CPU(\六十进制计数器_1_out_9 ), .QB(\四位二进制可逆计数器_1_qa [1]),
    .QC(\四位二进制可逆计数器_1_qa [2]), .QD(\四位二进制可逆计数器_1_qa [3]), .CLR(in_2), .D(1'b0), .C(1'b0), .B(1'b0), .A(1'b0));  // open: nLD
endmodule

module \十二进制计数器或二十四进制的计数器电路  (
  input  in_1,
  input  in_2,
  input  in_3,
  input  in_4,
  input  in_5,
  output out_6,
  output out_7,
  output out_8,
  output out_9,
  output out_10,
  output out_11,
  output out_12,
  output out_13,
  output out_14
);

  wire and_1_out, and_2_out, or_1_out;

  \六十进制计数器  \u_六十进制计数器_1  (
    .CPU(in_3), .out_5(out_10), .out_6(out_11), .out_7(out_12), .out_8(out_13), .out_10(out_6),
    .out_11(out_7), .out_12(out_8), .out_13(out_9), .Clr(or_1_out), .CPD(in_5), .Adj(in_4));  // open: out_9
  and and_1 (and_1_out, out_8, out_11);
  and and_2 (and_2_out, out_9, out_12);
  Multiplexer #(.select(1), .width(1), .disabled("Z"), .enable("false")) multiplexer_1 (
    .in0(and_2_out), .in1(and_1_out), .out(out_14), .sel(in_1));
  or or_1 (or_1_out, out_14, in_2);
endmodule

module \十二进制计数器或二十四进制的计数器测试电路  (
  input  in_1,
  input  in_2,
  input  in_3,
  input  in_4,
  input  in_5,
  output out_6
);

  wire clock_1_out, or_1_out, \十二进制计数器或二十四进制的计数器电路_1_out_14 , \四位二进制可逆计数器_1_qb ;
  wire [3:0] \十二进制计数器或二十四进制的计数器电路_1_out_9 , \十二进制计数器或二十四进制的计数器电路_1_out_13 ;

  Clock #(.highDuration(1), .lowDuration(1)) clock_1 (.out(clock_1_out));
  Hex_Digit_Display hex_digit_display_1 (.value(\十二进制计数器或二十四进制的计数器电路_1_out_9 ));  // open: dp
  Hex_Digit_Display hex_digit_display_2 (.value(\十二进制计数器或二十四进制的计数器电路_1_out_13 ));  // open: dp
  \十二进制计数器或二十四进制的计数器电路  \u_十二进制计数器或二十四进制的计数器电路_1  (
    .in_1(in_4), .in_3(clock_1_out), .out_14(\十二进制计数器或二十四进制的计数器电路_1_out_14 ), .in_4(in_1), .in_5(in_2),
    .in_2(in_3), .out_6(\十二进制计数器或二十四进制的计数器电路_1_out_9 [3]), .out_7(\十二进制计数器或二十四进制的计数器电路_1_out_9 [2]),
    .out_8(\十二进制计数器或二十四进制的计数器电路_1_out_9 [1]), .out_9(\十二进制计数器或二十四进制的计数器电路_1_out_9 [0]),
    .out_10(\十二进制计数器或二十四进制的计数器电路_1_out_13 [3]), .out_11(\十二进制计数器或二十四进制的计数器电路_1_out_13 [2]),
    .out_12(\十二进制计数器或二十四进制的计数器电路_1_out_13 [1]), .out_13(\十二进制计数器或二十四进制的计数器电路_1_out_13 [0]));
  or or_1 (or_1_out, \四位二进制可逆计数器_1_qb , in_3);
  \四位二进制可逆计数器  \u_四位二进制可逆计数器_1  (
    .CPD(in_5), .QA(out_6), .CPU(\十二进制计数器或二十四进制的计数器电路_1_out_14 ), .QB(\四位二进制可逆计数器_1_qb ), .CLR(or_1_out),
    .nLD(1'b1), .D(1'b0), .C(1'b0), .B(1'b0), .A(1'b0));  // open: QC, QD
endmodule

module \上下午文字显示的电路  (
  input  AM_PM,
  input  TT,
  output [6:0] out_3,
  output [6:0] out_4,
  output [6:0] out_5,
  output [6:0] out_6
);

  wire [27:0] multiplexer_1_out;

  Multiplexer #(.select(1), .width(28), .disabled("Z"), .enable("false")) multiplexer_1 (
    .in0(28'h207f89), .in1(28'h8103fc8), .out(multiplexer_1_out), .sel(AM_PM));
  Multiplexer #(.select(1), .width(28), .disabled("Z"), .enable("false")) multiplexer_2 (
    .in0({28{1'b0}}), .in1(multiplexer_1_out), .out({out_3, out_4, out_5, out_6}), .sel(TT));
endmodule

module \上下午文字显示测试电路  (
  input  AM_PM,
  input  TT
);

  wire [6:0] \上下午文字显示的电路_1_out_3 , \上下午文字显示的电路_1_out_4 , \上下午文字显示的电路_1_out_5 , \上下午文字显示的电路_1_out_6 ;

  DotMatrix #(.inputtype("column"), .matrixcols(5), .matrixrows(7), .persist(0), .dotshape("square")) dotmatrix_1 (
    .col0(\上下午文字显示的电路_1_out_3 ), .col1(\上下午文字显示的电路_1_out_4 ), .col2(\上下午文字显示的电路_1_out_5 ),
    .col3(\上下午文字显示的电路_1_out_6 ), .col4(\上下午文字显示的电路_1_out_6 ));
  \上下午文字显示的电路  \u_上下午文字显示的电路_1  (
    .out_3(\上下午文字显示的电路_1_out_3 ), .out_4(\上下午文字显示的电路_1_out_4 ), .out_5(\上下午文字显示的电路_1_out_5 ),
    .out_6(\上下午文字显示的电路_1_out_6 ), .AM_PM(AM_PM), .TT(TT));
endmodule

module \电子钟整点报时电路  (
  input  CPU,
  input  Adj,
  input  SET,
  input  CPD,
  input  CLR,
  output [3:0] out_6,
  output [3:0] out_7,
  output [3:0] out_8,
  output [3:0] out_9,
  output [3:0] out_10,
  output [3:0] out_11,
  output out_12
);

  wire \六十进制计数器_1_out_9 , \六十进制计数器_2_out_9 ;

  \六十进制计数器  \u_六十进制计数器_1  (
    .CPU(CPU), .out_5(out_7[3]), .out_6(out_7[2]), .out_7(out_7[1]), .out_8(out_7[0]),
    .out_9(\六十进制计数器_1_out_9 ), .out_10(out_6[3]), .out_11(out_6[2]), .out_12(out_6[1]), .out_13(out_6[0]),
    .Clr(CLR), .CPD(CPD), .Adj(Adj));
  \六十进制计数器  \u_六十进制计数器_2  (
    .CPU(\六十进制计数器_1_out_9 ), .out_5(out_9[3]), .out_6(out_9[2]), .out_7(out_9[1]), .out_8(out_9[0]),
    .out_9(\六十进制计数器_2_out_9 ), .out_10(out_8[3]), .out_11(out_8[2]), .out_12(out_8[1]), .out_13(out_8[0]),
    .Clr(CLR), .CPD(CPD), .Adj(Adj));
  and and_1 (out_12, out_8[2], out_8[0], out_9[3], out_9[0], out_6[2], out_6[0]);
  \十二进制计数器或二十四进制的计数器电路  \u_十二进制计数器或二十四进制的计数器电路_1  (
    .in_1(SET), .in_3(\六十进制计数器_2_out_9 ), .in_4(Adj), .in_5(CPD), .in_2(CLR), .out_6(out_10[3]),
    .out_7(out_10[2]), .out_8(out_10[1]), .out_9(out_10[0]), .out_10(out_11[3]), .out_11(out_11[2]),
    .out_12(out_11[1]), .out_13(out_11[0]));  // open: out_14
endmodule

module \电子钟整点报时电路测试电路  (
  input  in_1,
  input  in_2,
  input  in_3,
  input  in_4
);

  wire clock_1_out, \电子钟整点报时电路_1_out_12 ;
  wire [3:0] \电子钟整点报时电路_1_out_6 , \电子钟整点报时电路_1_out_7 , \电子钟整点报时电路_1_out_8 , \电子钟整点报时电路_1_out_9 ,
       \电子钟整点报时电路_1_out_10 , \电子钟整点报时电路_1_out_11 ;

  Clock #(.highDuration(1), .lowDuration(1)) clock_1 (.out(clock_1_out));
  Hex_Digit_Display hex_digit_display_1 (.value(\电子钟整点报时电路_1_out_10 ));  // open: dp
  Hex_Digit_Display hex_digit_display_2 (.value(\电子钟整点报时电路_1_out_11 ));  // open: dp
  Hex_Digit_Display hex_digit_display_3 (.value(\电子钟整点报时电路_1_out_9 ));  // open: dp
  Hex_Digit_Display hex_digit_display_4 (.value(\电子钟整点报时电路_1_out_8 ));  // open: dp
  \电子钟整点报时电路  \u_电子钟整点报时电路_1  (
    .CPU(clock_1_out), .Adj(in_1), .CPD(in_3), .CLR(in_4), .out_12(\电子钟整点报时电路_1_out_12 ), .SET(in_2),
    .out_6(\电子钟整点报时电路_1_out_6 ), .out_7(\电子钟整点报时电路_1_out_7 ), .out_8(\电子钟整点报时电路_1_out_8 ),
    .out_9(\电子钟整点报时电路_1_out_9 ), .out_10(\电子钟整点报时电路_1_out_10 ), .out_11(\电子钟整点报时电路_1_out_11 ));
  Hex_Digit_Display hex_digit_display_5 (.value(\电子钟整点报时电路_1_out_6 ));  // open: dp
  Hex_Digit_Display hex_digit_display_6 (.value(\电子钟整点报时电路_1_out_7 ));  // open: dp
  LED #(.active("true")) led_1 (.in(\电子钟整点报时电路_1_out_12 ));
endmodule

module \秒脉冲产生电路  (
  input  in_1,
  output out_2
);

  \四位二进制可逆计数器  \u_四位二进制可逆计数器_1  (
    .CPD(1'b0), .CPU(in_1), .QD(out_2), .CLR(out_2), .nLD(1'b1), .D(1'b0), .C(1'b0), .B(1'b0), .A(1'b0));  // open: QA, QB, QC
endmodule

module \多功能数字钟电路  (
  input  in_1,
  input  CPD,
  input  CLR,
  input  CPU,
  input  SET,
  input  Adj0,
  input  Adj1,
  output [3:0] out_8,
  output [3:0] out_9,
  output [3:0] out_10,
  output [3:0] out_11,
  output [3:0] out_12,
  output [3:0] out_13,
  output [6:0] out_14,
  output [6:0] out_15,
  output [6:0] out_16,
  output [6:0] out_17,
  output out_18
);

  wire and_1_out, and_2_out, d_ff_1_q, d_ff_1_qn, multiplexer_1_out, multiplexer_2_out, multiplexer_3_out,
       multiplexer_4_out, multiplexer_5_out, multiplexer_6_out, not_1_out, not_2_out, \六十进制计数器_1_out_9 ,
       \六十进制计数器_2_out_9 , \十二进制计数器或二十四进制的计数器电路_1_out_14 , \秒脉冲产生电路_1_out_2 ;

  \秒脉冲产生电路  \u_秒脉冲产生电路_1  (.in_1(in_1), .out_2(\秒脉冲产生电路_1_out_2 ));
  not not_1 (not_1_out, Adj1);
  \六十进制计数器  \u_六十进制计数器_1  (
    .CPU(\秒脉冲产生电路_1_out_2 ), .out_5(out_9[3]), .out_6(out_9[2]), .out_7(out_9[1]), .out_8(out_9[0]),
    .out_9(\六十进制计数器_1_out_9 ), .out_10(out_8[3]), .out_11(out_8[2]), .out_12(out_8[1]), .out_13(out_8[0]),
    .Clr(CLR), .CPD(1'b0), .Adj(1'b0));
  and and_1 (and_1_out, Adj0, Adj1);
  and and_2 (and_2_out, Adj0, not_1_out);
  Multiplexer #(.select(1), .width(1), .disabled("Z"), .enable("false")) multiplexer_1 (
    .in0(1'b0), .in1(CPD), .out(multiplexer_1_out), .sel(and_1_out));
  Multiplexer #(.select(1), .width(1), .disabled("Z"), .enable("false")) multiplexer_2 (
    .in0(\六十进制计数器_1_out_9 ), .in1(1'b0), .out(multiplexer_2_out), .sel(Adj0));
  Multiplexer #(.select(1), .width(1), .disabled("Z"), .enable("false")) multiplexer_3 (
    .in0(multiplexer_2_out), .in1(CPU), .out(multiplexer_3_out), .sel(and_1_out));
  \六十进制计数器  \u_六十进制计数器_2  (
    .CPU(multiplexer_3_out), .out_5(out_11[3]), .out_6(out_11[2]), .out_7(out_11[1]), .out_8(out_11[0]),
    .out_9(\六十进制计数器_2_out_9 ), .out_10(out_10[3]), .out_11(out_10[2]), .out_12(out_10[1]),
    .out_13(out_10[0]), .Clr(CLR), .CPD(multiplexer_1_out), .Adj(and_1_out));
  and and_3 (out_18, out_8[2], out_8[0], out_10[2], out_10[0], out_11[3], out_11[0]);
  Multiplexer #(.select(1), .width(1), .disabled("Z"), .enable("false")) multiplexer_4 (
    .in0(\六十进制计数器_2_out_9 ), .in1(1'b0), .out(multiplexer_4_out), .sel(and_1_out));
  Multiplexer #(.select(1), .width(1), .disabled("Z"), .enable("false")) multiplexer_5 (
    .in0(multiplexer_4_out), .in1(CPU), .out(multiplexer_5_out), .sel(and_2_out));
  Multiplexer #(.select(1), .width(1), .disabled("Z"), .enable("false")) multiplexer_6 (
    .in0(1'b0), .in1(CPD), .out(multiplexer_6_out), .sel(and_2_out));
  \十二进制计数器或二十四进制的计数器电路  \u_十二进制计数器或二十四进制的计数器电路_1  (
    .in_1(SET), .in_3(multiplexer_5_out), .out_14(\十二进制计数器或二十四进制的计数器电路_1_out_14 ), .in_4(and_2_out),
    .in_5(multiplexer_6_out), .in_2(CLR), .out_6(out_12[3]), .out_7(out_12[2]), .out_8(out_12[1]),
    .out_9(out_12[0]), .out_10(out_13[3]), .out_11(out_13[2]), .out_12(out_13[1]), .out_13(out_13[0]));
  D_Flip_Flop #(.trigger("falling"), .Pre_Clr_Positions("ABOVE_BELOW"), .NegatePresetClear("false"), .enable("false"), .NewFFLayout("true")) d_ff_1 (
    .clk(\十二进制计数器或二十四进制的计数器电路_1_out_14 ), .D(d_ff_1_qn), .Q(d_ff_1_q), .Qn(d_ff_1_qn), .reset(CLR));  // open: preset
  \上下午文字显示的电路  \u_上下午文字显示的电路_1  (
    .out_3(out_14), .out_4(out_15), .out_5(out_16), .out_6(out_17), .AM_PM(d_ff_1_q), .TT(not_2_out));
  not not_2 (not_2_out, SET);
endmodule

module \多功能数字钟测试电路  (
  input  in_1,
  input  in_2,
  input  in_3,
  input  in_4,
  input  in_5
);

  wire button_1_out, clock_1_out, \多功能数字钟电路_1_out_18 ;
  wire [3:0] \多功能数字钟电路_1_out_8 , \多功能数字钟电路_1_out_9 , \多功能数字钟电路_1_out_10 , \多功能数字钟电路_1_out_11 ,
       \多功能数字钟电路_1_out_12 , \多功能数字钟电路_1_out_13 ;
  wire [6:0] \多功能数字钟电路_1_out_14 , \多功能数字钟电路_1_out_15 , \多功能数字钟电路_1_out_16 , \多功能数字钟电路_1_out_17 ;

  DotMatrix #(.inputtype("column"), .matrixcols(5), .matrixrows(7), .persist(0), .dotshape("square")) dotmatrix_1 (
    .col0(\多功能数字钟电路_1_out_14 ), .col1(\多功能数字钟电路_1_out_15 ), .col2(\多功能数字钟电路_1_out_16 ),
    .col3(\多功能数字钟电路_1_out_17 ), .col4(\多功能数字钟电路_1_out_17 ));
  Hex_Digit_Display hex_digit_display_1 (.value(\多功能数字钟电路_1_out_12 ));  // open: dp
  \多功能数字钟电路  \u_多功能数字钟电路_1  (
    .CPD(in_3), .CLR(in_5), .CPU(button_1_out), .Adj0(in_1), .Adj1(in_2), .out_18(\多功能数字钟电路_1_out_18 ),
    .out_8(\多功能数字钟电路_1_out_8 ), .out_9(\多功能数字钟电路_1_out_9 ), .out_10(\多功能数字钟电路_1_out_10 ),
    .out_11(\多功能数字钟电路_1_out_11 ), .out_14(\多功能数字钟电路_1_out_14 ), .out_15(\多功能数字钟电路_1_out_15 ),
    .out_16(\多功能数字钟电路_1_out_16 ), .out_17(\多功能数字钟电路_1_out_17 ), .SET(in_4), .in_1(clock_1_out),
    .out_12(\多功能数字钟电路_1_out_12 ), .out_13(\多功能数字钟电路_1_out_13 ));
  Button button_1 (.out(button_1_out));
  Clock #(.highDuration(1), .lowDuration(1)) clock_1 (.out(clock_1_out));
  Hex_Digit_Display hex_digit_display_2 (.value(\多功能数字钟电路_1_out_13 ));  // open: dp
  Hex_Digit_Display hex_digit_display_3 (.value(\多功能数字钟电路_1_out_10 ));  // open: dp
  Hex_Digit_Display hex_digit_display_4 (.value(\多功能数字钟电路_1_out_11 ));  // open: dp
  Hex_Digit_Display hex_digit_display_5 (.value(\多功能数字钟电路_1_out_8 ));  // open: dp
  Hex_Digit_Display hex_digit_display_6 (.value(\多功能数字钟电路_1_out_9 ));  // open: dp
  LED #(.active("true")) led_1 (.in(\多功能数字钟电路_1_out_18 ));
  // Buzzer #(.freq_measure("Hz"), .vol_width(7)) buzzer_1: pin names not known; wires that end beside it: \多功能数字钟电路_1_out_18 
endmodule
